// Logisim project cpu21-riscv.circ as structural Verilog: 19 circuits, main circuit ◇单周期RISC-V
module \单周期RISC_V  (
  input  IR1,
  input  IR2,
  input  IR3,
  output RegWrite,
  output MemWrite,
  output [31:0] PC,
  output [31:0] IR,
  output [31:0] RDin,
  output [31:0] MDin,
  output [31:0] LedData
);

  wire ALU, ALUEquals, and_1_out, and_2_out, and_3_out, and_4_out, Beq, BLTU, Bne, button_1_out, CLK,
       clock_2_out, comparator_1_eq, comparator_2_eq, comparator_2_lt, d_ff_2_q, ecall, Go, halt, IR1_t,
       IR2_t, IR3_t, IRA, IRB, IRC, JAL, Jalr, LH, LUI, nand_1_out, not_1_out, not_2_out, not_3_out,
       or_1_out, riscv_probe_1_p2, RST, S, W1, W2, W3, \单周期硬布线控制器_1_alu_src ;
  wire [1:0] priority_encoder_1_out, \单周期硬布线控制器_1_memtoreg ;
  wire [3:0] \单周期硬布线控制器_1_alu_op ;
  wire [4:0] multiplexer_2_out, multiplexer_3_out;
  wire [12:0] CNT_num;
  wire [15:0] multiplexer_8_out, \总周期数 ;
  wire [31:0] adder_2_out, adder_3_out, ALUResult, bit_extender_1_out, bit_extender_2_out,
       bit_extender_3_out, bit_extender_4_out, DataOut, LHExdendedData, multiplexer_1_out, multiplexer_4_out,
       multiplexer_6_out, multiplexer_7_out, multiplexer_9_out, PC_4, regifile_1_r1, shifter_1_out,
       shifter_2_out;

  Clock #(.highDuration(1), .lowDuration(1)) clock_1 ();  // open: out
  Button _1 (.out(IRA));
  Button _2 (.out(IRB));
  Button _3 (.out(IRC));
  Button \u_继续运行  (.out(Go));
  LED #(.active("true")) led_1 (.in(W1));
  LED #(.active("true")) led_2 (.in(W2));
  LED #(.active("true")) led_3 (.in(W3));
  Hex_Digit_Display hex_digit_display_1 (.value(LedData[31:28]));  // open: dp
  Priority_Encoder #(.select(2), .disabled("Z")) priority_encoder_1 (
    .in0(1'b1), .in1(Jalr), .in2(JAL), .in3(or_1_out), .out(priority_encoder_1_out));  // open: gs, en_out, en_in
  Register #(.width(32), .trigger("rising"), .Select("low")) u_PC (
    .D(multiplexer_1_out), .en(not_1_out), .Q(PC), .clk(CLK), .clr(RST));
  Multiplexer #(.select(2), .width(32), .disabled("Z"), .enable("false")) multiplexer_1 (
    .in0(PC_4), .in1(ALUResult), .in2(adder_3_out), .in3(adder_2_out), .out(multiplexer_1_out),
    .sel(priority_encoder_1_out));
  not not_1 (not_1_out, halt);
  Hex_Digit_Display hex_digit_display_2 (.value(LedData[23:20]));  // open: dp
  Hex_Digit_Display hex_digit_display_3 (.value(LedData[27:24]));  // open: dp
  and and_1 (and_1_out, Beq, ALUEquals);
  and and_2 (and_2_out, ~ALUEquals, Bne);  // AND_Gate
  or or_1 (or_1_out, and_1_out, and_2_out, and_3_out);
  and and_3 (and_3_out, ALU, BLTU);
  Hex_Digit_Display hex_digit_display_4 (.value(LedData[15:12]));  // open: dp
  Hex_Digit_Display hex_digit_display_5 (.value(LedData[19:16]));  // open: dp
  // RiscV_Probe riscv_probe_1: pin names not known; wires that end beside it: IR, riscv_probe_1_p2
  Adder #(.width(32)) adder_1 (.a(PC), .b(32'h4), .out(PC_4));  // open: cin, cout
  Hex_Digit_Display hex_digit_display_6 (.value(LedData[11:8]));  // open: dp
  Hex_Digit_Display hex_digit_display_7 (.value(LedData[7:4]));  // open: dp
  // Probe on \总周期数 
  ROM #(.addrWidth(10), .dataWidth(32), .Select("high")) rom_1 (.addr(PC[11:2]), .data(IR));
  Hex_Digit_Display hex_digit_display_8 (.value(LedData[3:0]));  // open: dp
  \单周期硬布线控制器  \u_单周期硬布线控制器_1  (
    .Funct({IR[30], IR[25], IR[14:12]}), .OP(IR[6:2]), .ALU_OP(\单周期硬布线控制器_1_alu_op ),
    .MemToReg(\单周期硬布线控制器_1_memtoreg [0]), .MemWrite(MemWrite), .ALU_SRC(\单周期硬布线控制器_1_alu_src ),
    .RegWrite(RegWrite), .ecall(ecall), .S_type(S), .Jalr(Jalr), .Beq(Beq), .JAL(JAL), .Bne(Bne),
    .BLTU(BLTU), .XOR(riscv_probe_1_p2), .LUI(LUI), .LH(LH), .in_3(IR[21]));  // open: RS1_USED, RS2_USED, uret
  or or_2 (IR1_t, IR1, IRA);
  Multiplexer #(.select(1), .width(5), .disabled("Z"), .enable("false")) multiplexer_2 (
    .in0(IR[19:15]), .in1(5'b10001), .out(multiplexer_2_out), .sel(ecall));
  Multiplexer #(.select(1), .width(5), .disabled("Z"), .enable("false")) multiplexer_3 (
    .in0(IR[24:20]), .in1(5'b01010), .out(multiplexer_3_out), .sel(ecall));
  assign bit_extender_1_out = {{20{IR[31]}}, IR[31:20]};  // Bit_Extender bit_extender_1
  assign bit_extender_2_out = {{20{IR[31]}}, {IR[31:25], IR[11:7]}};  // Bit_Extender bit_extender_2
  assign bit_extender_3_out = {{20{IR[31]}}, {IR[31], IR[7], IR[30:25], IR[11:8]}};  // Bit_Extender bit_extender_3
  assign bit_extender_4_out = {{12{IR[31]}}, {IR[31], IR[19:12], IR[20], IR[30:21]}};  // Bit_Extender bit_extender_4
  or or_3 (IR2_t, IR2, IRB);
  // Probe on multiplexer_2_out
  // Probe on multiplexer_3_out
  // Probe on IR[11:7]
  Multiplexer #(.select(1), .width(32), .disabled("Z"), .enable("false")) multiplexer_4 (
    .in0(bit_extender_1_out), .in1(bit_extender_2_out), .out(multiplexer_4_out), .sel(S));
  Shifter #(.width(32), .shift("ll")) shifter_1 (.in(bit_extender_3_out), .\dist (5'b00001), .out(shifter_1_out));
  Adder #(.width(32)) adder_2 (.a(shifter_1_out), .b(PC), .out(adder_2_out));  // open: cin, cout
  Shifter #(.width(32), .shift("ll")) shifter_2 (.in(bit_extender_4_out), .\dist (5'b00001), .out(shifter_2_out));
  Adder #(.width(32)) adder_3 (.a(shifter_2_out), .b(PC), .out(adder_3_out));  // open: cin, cout
  not not_2 (not_2_out, halt);
  Counter #(.width(16), .max('hffff), .ongoal("wrap"), .trigger("rising"), .behavior("new")) counter_1 (
    .count(not_2_out), .Q(\总周期数 ), .clk(CLK));  // open: load, D, carry, clr, preset, down
  Multiplexer #(.select(1), .width(32), .disabled("Z"), .enable("false")) multiplexer_5 (
    .in0(multiplexer_9_out), .in1({IR[31:12], {12{1'b0}}}), .out(RDin), .sel(LUI));
  or or_4 (IR3_t, IR3, IRC);
  Regifile regifile_1 (
    .Din(RDin), .Clk(CLK), .R1(regifile_1_r1), .R2(MDin), .WE(RegWrite), .W_num(IR[11:7]),
    .R1_num(multiplexer_2_out), .R2_num(multiplexer_3_out));
  Multiplexer #(.select(1), .width(32), .disabled("Z"), .enable("false")) multiplexer_6 (
    .in0(MDin), .in1(multiplexer_4_out), .out(multiplexer_6_out), .sel(\单周期硬布线控制器_1_alu_src ));
  ALU alu_1 (
    .X(regifile_1_r1), .Y(multiplexer_6_out), .AluOP(\单周期硬布线控制器_1_alu_op ), .Equal(ALUEquals),
    .Result(ALUResult), .out_6(ALU));  // open: Result_2, out_4
  Comparator #(.width(32), .mode("twosComplement")) comparator_1 (
    .a(regifile_1_r1), .b(32'ha), .eq(comparator_1_eq));  // open: gt, lt
  not not_3 (not_3_out, comparator_1_eq);
  and and_4 (and_4_out, not_3_out, ecall);
  D_Flip_Flop #(.trigger("rising"), .Pre_Clr_Positions("ABOVE_BELOW"), .NegatePresetClear("false"), .enable("true"), .NewFFLayout("true")) d_ff_1 (
    .clk(comparator_1_eq), .D(1'b1), .Q(halt), .en(ecall), .reset(Go));  // open: Qn, preset
  Register #(.width(32), .trigger("rising"), .Select("low")) PC_2 (
    .D(MDin), .en(and_4_out), .Q(LedData), .clk(CLK));  // open: clr
  Button button_1 (.out(button_1_out));
  RAM #(.addrWidth(10), .dataWidth(32), .bus("separate"), .Select("high")) ram_1 (
    .addr(ALUResult[11:2]), .din(MDin), .data(DataOut), .str(MemWrite), .sel(1'b1), .clk(CLK), .ld(1'b1),
    .clr(button_1_out));
  D_Flip_Flop #(.trigger("high"), .Pre_Clr_Positions("LEGACY"), .NegatePresetClear("false"), .enable("true"), .NewFFLayout("false")) d_ff_2 (.Q(d_ff_2_q));  // open: clk, D, Qn, preset, en, reset
  // Probe on 13'hc
  Multiplexer #(.select(1), .width(32), .disabled("Z"), .enable("false")) multiplexer_7 (
    .in0(DataOut), .in1(LHExdendedData), .out(multiplexer_7_out), .sel(LH));
  Multiplexer #(.select(1), .width(16), .disabled("Z"), .enable("false")) multiplexer_8 (
    .in0(DataOut[15:0]), .in1(DataOut[31:16]), .out(multiplexer_8_out), .sel(ALUResult[1]));
  Comparator #(.width(13), .mode("twosComplement")) comparator_2 (
    .a(CNT_num), .b(13'hc), .eq(comparator_2_eq), .lt(comparator_2_lt));  // open: gt
  Clock #(.highDuration(1), .lowDuration(1)) clock_2 (.out(clock_2_out));
  or or_5 (\单周期硬布线控制器_1_memtoreg [1], JAL, Jalr);
  Multiplexer #(.select(2), .width(32), .disabled("Z"), .enable("false")) multiplexer_9 (
    .in0(ALUResult), .in1(multiplexer_7_out), .in2(PC_4), .out(multiplexer_9_out),
    .sel(\单周期硬布线控制器_1_memtoreg ));  // open: in3
  assign LHExdendedData = {{16{multiplexer_8_out[15]}}, multiplexer_8_out};  // Bit_Extender bit_extender_5
  Counter #(.width(13), .max('h1fff), .ongoal("stay"), .trigger("rising"), .behavior("old")) counter_2 (
    .count(comparator_2_lt), .Q(CNT_num), .clk(clock_2_out));  // open: load, D, carry, clr, preset
  nand nand_1 (nand_1_out, d_ff_2_q, comparator_2_eq);
  assign CLK = nand_1_out ? clock_2_out : 1'bz;  // Controlled_Buffer controlled_buffer_1
  Pull_Resistor #(.pull(1)) pull_resistor_1 (.node(CLK));

  // Notes on the sheet:
  //   中断源
  //   中断等待指示
  //   总复位信号应将除ROM以外所有存储组件全部清零
  //   BLTU 指令支持电路
  //   数码管输出
  //   指令存储器
  //   数码管输出应该用寄存器锁存，否则显示数据只能一闪而过
  //   指令字
  //   contents of rom_1 (hex, n*v repeats v):
  //   313 1000e13 8400493 849493 8348493 400913 891913 490913 849493 8248493 849493 8148493 891913 490913
  //   891913 490913 932023 12484b3 430313 fffe0e13 fe0e18e3 2000e13 313 31483 900533 2200893 73 230313
  //   fffe0e13 fe0e14e3 a00893 73
  //   JAL
  //   Jalr
  //   XOR
  //   LUI
  //   LH
  //   BLTU
  //   rs1
  //   rs2
  //   rd
  //   Beq
  //   Bne
  //   MemToReg
  //   MemWrite
  //   AluOP
  //   AluSrcB
  //   RegWrite
  //   Stype
  //   ecall
  //   imm12
  //   imm_sw
  //   imm_b
  //   imm_j
  //   LUI 指令支持电路
  //   为方便自动评测，需要输出PC，IR，寄存器堆写如数据RDin
  //   RAM写使能MemWrite、RAM写入数据MDin等信号
  //   数据存储器
  //   控制位
  //   暂停节拍，不能为0
  //   戳工具置1进入计数暂停模式，ctrl+k时钟自动运行到对应节拍暂停
  //   ctrl+k关闭时钟连续运行，将控制位置零，进入单步调试模式调试
  //   用这个时钟源需要去掉电路中的其他时钟源
  //   LH 指令支持电路
  //   可计数暂停的时钟源
endmodule

// 单周期硬布线控制器
module \单周期硬布线控制器  (
  input  [4:0] OP,
  input  [4:0] Funct,
  input  in_3,
  output [3:0] ALU_OP,
  output ecall,
  output uret,
  output MemToReg,
  output MemWrite,
  output ALU_SRC,
  output RegWrite,
  output S_type,
  output Beq,
  output Bne,
  output Jalr,
  output JAL,
  output XOR,
  output LUI,
  output LH,
  output BLTU,
  output RS1_USED,
  output RS2_USED
);

  wire \控制信号自动生成_1_ecall ;

  \运算控制器自动生成  \u_运算控制器自动生成_1  (
    .OP2(OP[0]), .OP3(OP[1]), .OP4(OP[2]), .OP5(OP[3]), .OP6(OP[4]), .F12(Funct[0]), .F13(Funct[1]),
    .F14(Funct[2]), .F25(Funct[3]), .F30(Funct[4]), .S0(ALU_OP[0]), .S1(ALU_OP[1]), .S2(ALU_OP[2]),
    .S3(ALU_OP[3]));
  \控制信号自动生成  \u_控制信号自动生成_1  (
    .OP2(OP[0]), .OP3(OP[1]), .OP4(OP[2]), .OP5(OP[3]), .OP6(OP[4]), .MemToReg(MemToReg), .F12(Funct[0]),
    .F13(Funct[1]), .F14(Funct[2]), .F25(Funct[3]), .F30(Funct[4]), .MemWrite(MemWrite), .ALU_SRC(ALU_SRC),
    .RegWrite(RegWrite), .ecall(\控制信号自动生成_1_ecall ), .S_Type(S_type), .BEQ(Beq), .BNE(Bne), .JALR(Jalr),
    .JAL(JAL), .XOR(XOR), .LUI(LUI), .LH(LH), .BLTU(BLTU), .RS1_USED(RS1_USED), .RS2_USED(RS2_USED));
  Demultiplexer #(.select(1), .width(1), .tristate("false"), .disabled("Z"), .enable("false")) demultiplexer_1 (
    .out0(ecall), .out1(uret), .in(\控制信号自动生成_1_ecall ), .sel(in_3));

  // Other names for the same wires on the sheet: OP_CODE[4:0] = OP

  // Notes on the sheet:
  //   控制信号生成，产生数据通路需要的其他控制信号
  //   运算器控制器，根据指令生成运算器功能选择信号
endmodule

// 运算器控制器
module \运算控制器自动生成  (
  input  OP2,
  input  OP3,
  input  OP4,
  input  OP5,
  input  OP6,
  input  F12,
  input  F13,
  input  F14,
  input  F25,
  input  F30,
  output S0,
  output S1,
  output S2,
  output S3
);

  wire and_1_out, and_2_out, and_3_out, and_4_out, and_5_out, and_6_out, and_7_out, and_8_out, and_9_out,
       and_10_out, and_11_out, and_12_out, and_13_out, and_14_out, and_15_out, and_16_out, and_17_out,
       and_18_out, and_19_out, and_20_out, and_21_out, and_22_out, and_23_out, and_24_out, and_25_out,
       and_26_out, and_27_out, and_28_out, and_29_out, and_30_out, and_31_out, and_32_out, and_33_out,
       and_34_out, and_35_out, and_36_out, not_1_out, not_2_out, not_3_out, not_4_out, not_5_out, not_6_out,
       not_7_out, not_8_out, not_9_out, not_10_out, not_11_out, not_12_out, not_13_out, not_14_out,
       not_15_out, not_16_out, not_17_out, not_18_out, not_19_out, not_20_out, not_21_out, not_22_out,
       not_23_out, not_24_out, not_25_out, not_26_out, not_27_out, not_28_out, not_29_out, not_30_out,
       not_31_out, not_32_out, not_33_out, not_34_out, not_35_out, not_36_out, not_37_out, not_38_out,
       not_39_out, not_40_out, not_41_out, not_42_out, not_43_out, not_44_out, not_45_out, not_46_out,
       not_47_out, not_48_out, not_49_out, not_50_out, not_51_out, not_52_out, not_53_out, not_54_out,
       not_55_out, not_56_out, not_57_out, not_58_out, not_59_out, not_60_out, not_61_out, not_62_out,
       not_63_out, not_64_out, not_65_out, not_66_out, not_67_out, not_68_out, not_69_out, not_70_out,
       not_71_out, not_72_out, not_73_out, not_74_out, not_75_out, not_76_out, not_77_out, not_78_out,
       not_79_out, not_80_out, not_81_out, not_82_out, not_83_out, not_84_out, not_85_out, not_86_out,
       not_87_out, not_88_out, not_89_out, not_90_out, not_91_out, not_92_out, not_93_out, not_94_out,
       not_95_out, not_96_out, not_97_out, not_98_out, not_99_out, not_100_out, not_101_out, not_102_out,
       not_103_out, not_104_out, not_105_out, not_106_out, not_107_out, not_108_out, not_109_out,
       not_110_out, not_111_out, not_112_out, not_113_out, not_114_out, not_115_out, not_116_out,
       not_117_out, not_118_out, not_119_out, not_120_out, not_121_out, not_122_out, not_123_out,
       not_124_out, not_125_out, not_126_out, not_127_out, not_128_out, not_129_out, not_130_out,
       not_131_out, not_132_out, not_133_out, not_134_out, not_135_out, not_136_out, not_137_out,
       not_138_out, not_139_out, not_140_out, not_141_out, not_142_out, not_143_out, not_144_out,
       not_145_out, not_146_out, not_147_out, not_148_out, not_149_out, not_150_out, not_151_out,
       not_152_out, not_153_out, not_154_out, not_155_out, not_156_out, not_157_out, not_158_out,
       not_159_out, not_160_out, not_161_out, not_162_out, not_163_out, not_164_out, not_165_out,
       not_166_out, not_167_out, not_168_out, not_169_out, not_170_out, not_171_out, not_172_out,
       not_173_out, not_174_out, not_175_out, not_176_out, not_177_out, not_178_out, not_179_out,
       not_180_out, not_181_out, not_182_out, not_183_out, not_184_out, not_185_out, not_186_out,
       not_187_out, not_188_out, not_189_out, not_190_out, not_191_out, not_192_out, not_193_out,
       not_194_out, not_195_out, not_196_out, not_197_out, not_198_out, not_199_out, not_200_out,
       not_201_out, not_202_out, not_203_out, not_204_out, not_205_out, not_206_out, not_207_out,
       not_208_out, not_209_out, not_210_out, not_211_out, not_212_out;

  not not_1 (not_1_out, F30);
  not not_2 (not_2_out, F25);
  not not_3 (not_3_out, F14);
  not not_4 (not_4_out, F13);
  not not_5 (not_5_out, F12);
  not not_6 (not_6_out, OP6);
  not not_7 (not_7_out, OP3);
  not not_8 (not_8_out, OP2);
  not not_9 (not_9_out, F30);
  not not_10 (not_10_out, F25);
  not not_11 (not_11_out, OP6);
  not not_12 (not_12_out, OP3);
  not not_13 (not_13_out, OP2);
  not not_14 (not_14_out, F30);
  not not_15 (not_15_out, F25);
  not not_16 (not_16_out, F14);
  not not_17 (not_17_out, F12);
  not not_18 (not_18_out, OP6);
  not not_19 (not_19_out, OP3);
  not not_20 (not_20_out, OP2);
  not not_21 (not_21_out, F14);
  not not_22 (not_22_out, F13);
  not not_23 (not_23_out, F12);
  not not_24 (not_24_out, OP6);
  not not_25 (not_25_out, OP5);
  not not_26 (not_26_out, OP3);
  not not_27 (not_27_out, OP2);
  not not_28 (not_28_out, OP6);
  not not_29 (not_29_out, OP5);
  not not_30 (not_30_out, OP3);
  not not_31 (not_31_out, OP2);
  not not_32 (not_32_out, F13);
  not not_33 (not_33_out, F12);
  not not_34 (not_34_out, OP6);
  not not_35 (not_35_out, OP5);
  not not_36 (not_36_out, OP3);
  not not_37 (not_37_out, OP2);
  not not_38 (not_38_out, F14);
  not not_39 (not_39_out, F12);
  not not_40 (not_40_out, OP6);
  not not_41 (not_41_out, OP5);
  not not_42 (not_42_out, OP3);
  not not_43 (not_43_out, OP2);
  not not_44 (not_44_out, F25);
  not not_45 (not_45_out, F13);
  not not_46 (not_46_out, OP6);
  not not_47 (not_47_out, OP5);
  not not_48 (not_48_out, OP3);
  not not_49 (not_49_out, OP2);
  not not_50 (not_50_out, F30);
  not not_51 (not_51_out, F25);
  not not_52 (not_52_out, F13);
  not not_53 (not_53_out, F12);
  not not_54 (not_54_out, OP6);
  not not_55 (not_55_out, OP3);
  not not_56 (not_56_out, OP2);
  not not_57 (not_57_out, F25);
  not not_58 (not_58_out, F14);
  not not_59 (not_59_out, F13);
  not not_60 (not_60_out, F12);
  not not_61 (not_61_out, OP6);
  not not_62 (not_62_out, OP3);
  not not_63 (not_63_out, OP2);
  not not_64 (not_64_out, F30);
  not not_65 (not_65_out, F25);
  not not_66 (not_66_out, OP6);
  not not_67 (not_67_out, OP3);
  not not_68 (not_68_out, OP2);
  not not_69 (not_69_out, F30);
  not not_70 (not_70_out, F25);
  not not_71 (not_71_out, F14);
  not not_72 (not_72_out, F12);
  not not_73 (not_73_out, OP6);
  not not_74 (not_74_out, OP3);
  not not_75 (not_75_out, OP2);
  not not_76 (not_76_out, OP6);
  not not_77 (not_77_out, OP5);
  not not_78 (not_78_out, OP3);
  not not_79 (not_79_out, OP2);
  not not_80 (not_80_out, F14);
  not not_81 (not_81_out, F12);
  not not_82 (not_82_out, OP6);
  not not_83 (not_83_out, OP5);
  not not_84 (not_84_out, OP3);
  not not_85 (not_85_out, OP2);
  not not_86 (not_86_out, F30);
  not not_87 (not_87_out, F25);
  not not_88 (not_88_out, F13);
  not not_89 (not_89_out, OP6);
  not not_90 (not_90_out, OP5);
  not not_91 (not_91_out, OP3);
  not not_92 (not_92_out, OP2);
  not not_93 (not_93_out, F14);
  not not_94 (not_94_out, F13);
  not not_95 (not_95_out, F12);
  not not_96 (not_96_out, OP4);
  not not_97 (not_97_out, OP3);
  not not_98 (not_98_out, OP2);
  not not_99 (not_99_out, F14);
  not not_100 (not_100_out, F13);
  not not_101 (not_101_out, OP4);
  not not_102 (not_102_out, OP3);
  not not_103 (not_103_out, OP2);
  not not_104 (not_104_out, F14);
  not not_105 (not_105_out, F13);
  not not_106 (not_106_out, F12);
  not not_107 (not_107_out, OP4);
  not not_108 (not_108_out, OP3);
  not not_109 (not_109_out, F30);
  not not_110 (not_110_out, F25);
  not not_111 (not_111_out, F14);
  not not_112 (not_112_out, F13);
  not not_113 (not_113_out, F12);
  not not_114 (not_114_out, OP6);
  not not_115 (not_115_out, OP3);
  not not_116 (not_116_out, OP2);
  not not_117 (not_117_out, F25);
  not not_118 (not_118_out, F14);
  not not_119 (not_119_out, F13);
  not not_120 (not_120_out, F12);
  not not_121 (not_121_out, OP6);
  not not_122 (not_122_out, OP3);
  not not_123 (not_123_out, OP2);
  not not_124 (not_124_out, F30);
  not not_125 (not_125_out, F25);
  not not_126 (not_126_out, OP6);
  not not_127 (not_127_out, OP3);
  not not_128 (not_128_out, OP2);
  not not_129 (not_129_out, F30);
  not not_130 (not_130_out, F25);
  not not_131 (not_131_out, F14);
  not not_132 (not_132_out, OP6);
  not not_133 (not_133_out, OP3);
  not not_134 (not_134_out, OP2);
  not not_135 (not_135_out, F14);
  not not_136 (not_136_out, F13);
  not not_137 (not_137_out, F12);
  not not_138 (not_138_out, OP6);
  not not_139 (not_139_out, OP5);
  not not_140 (not_140_out, OP3);
  not not_141 (not_141_out, OP2);
  not not_142 (not_142_out, OP6);
  not not_143 (not_143_out, OP5);
  not not_144 (not_144_out, OP3);
  not not_145 (not_145_out, OP2);
  not not_146 (not_146_out, F14);
  not not_147 (not_147_out, F13);
  not not_148 (not_148_out, F12);
  not not_149 (not_149_out, OP4);
  not not_150 (not_150_out, OP3);
  not not_151 (not_151_out, OP2);
  not not_152 (not_152_out, F14);
  not not_153 (not_153_out, F13);
  not not_154 (not_154_out, OP4);
  not not_155 (not_155_out, OP3);
  not not_156 (not_156_out, OP2);
  not not_157 (not_157_out, F14);
  not not_158 (not_158_out, F13);
  not not_159 (not_159_out, F12);
  not not_160 (not_160_out, OP4);
  not not_161 (not_161_out, OP3);
  not not_162 (not_162_out, F12);
  not not_163 (not_163_out, OP4);
  not not_164 (not_164_out, OP3);
  not not_165 (not_165_out, OP2);
  not not_166 (not_166_out, F30);
  not not_167 (not_167_out, F25);
  not not_168 (not_168_out, F12);
  not not_169 (not_169_out, OP6);
  not not_170 (not_170_out, OP3);
  not not_171 (not_171_out, OP2);
  not not_172 (not_172_out, F30);
  not not_173 (not_173_out, F25);
  not not_174 (not_174_out, F14);
  not not_175 (not_175_out, F12);
  not not_176 (not_176_out, OP6);
  not not_177 (not_177_out, OP3);
  not not_178 (not_178_out, OP2);
  not not_179 (not_179_out, F30);
  not not_180 (not_180_out, F25);
  not not_181 (not_181_out, F14);
  not not_182 (not_182_out, OP6);
  not not_183 (not_183_out, OP3);
  not not_184 (not_184_out, OP2);
  not not_185 (not_185_out, F12);
  not not_186 (not_186_out, OP6);
  not not_187 (not_187_out, OP5);
  not not_188 (not_188_out, OP3);
  not not_189 (not_189_out, OP2);
  not not_190 (not_190_out, F13);
  not not_191 (not_191_out, F12);
  not not_192 (not_192_out, OP6);
  not not_193 (not_193_out, OP5);
  not not_194 (not_194_out, OP3);
  not not_195 (not_195_out, OP2);
  not not_196 (not_196_out, F14);
  not not_197 (not_197_out, F12);
  not not_198 (not_198_out, OP6);
  not not_199 (not_199_out, OP5);
  not not_200 (not_200_out, OP3);
  not not_201 (not_201_out, OP2);
  not not_202 (not_202_out, F30);
  not not_203 (not_203_out, F25);
  not not_204 (not_204_out, F13);
  not not_205 (not_205_out, F12);
  not not_206 (not_206_out, OP6);
  not not_207 (not_207_out, OP3);
  not not_208 (not_208_out, OP2);
  not not_209 (not_209_out, F12);
  not not_210 (not_210_out, OP4);
  not not_211 (not_211_out, OP3);
  not not_212 (not_212_out, OP2);
  and and_1 (and_1_out, not_1_out, not_2_out, not_3_out, not_4_out, not_5_out, not_6_out, OP5, OP4, not_7_out, not_8_out);
  and and_2 (and_2_out, not_9_out, not_10_out, F14, F13, F12, not_11_out, OP5, OP4, not_12_out, not_13_out);
  and and_3 (and_3_out, not_14_out, not_15_out, not_16_out, F13, not_17_out, not_18_out, OP5, OP4, not_19_out, not_20_out);
  and and_4 (and_4_out, not_21_out, not_22_out, not_23_out, not_24_out, not_25_out, OP4, not_26_out, not_27_out);
  and and_5 (and_5_out, F14, F13, F12, not_28_out, not_29_out, OP4, not_30_out, not_31_out);
  and and_6 (and_6_out, F14, not_32_out, not_33_out, not_34_out, not_35_out, OP4, not_36_out, not_37_out);
  and and_7 (and_7_out, not_38_out, F13, not_39_out, not_40_out, not_41_out, OP4, not_42_out, not_43_out);
  and and_8 (and_8_out, F30, not_44_out, F14, not_45_out, F12, not_46_out, not_47_out, OP4, not_48_out, not_49_out);
  and and_9 (and_9_out, not_50_out, not_51_out, F14, not_52_out, not_53_out, not_54_out, OP5, OP4, not_55_out, not_56_out);
  and and_10 (and_10_out, F30, not_57_out, not_58_out, not_59_out, not_60_out, not_61_out, OP5, OP4, not_62_out, not_63_out);
  and and_11 (and_11_out, not_64_out, not_65_out, F14, F13, F12, not_66_out, OP5, OP4, not_67_out, not_68_out);
  and and_12 (and_12_out, not_69_out, not_70_out, not_71_out, F13, not_72_out, not_73_out, OP5, OP4, not_74_out, not_75_out);
  and and_13 (and_13_out, F14, F13, F12, not_76_out, not_77_out, OP4, not_78_out, not_79_out);
  and and_14 (and_14_out, not_80_out, F13, not_81_out, not_82_out, not_83_out, OP4, not_84_out, not_85_out);
  and and_15 (and_15_out, not_86_out, not_87_out, F14, not_88_out, F12, not_89_out, not_90_out, OP4, not_91_out, not_92_out);
  and and_16 (and_16_out, not_93_out, not_94_out, not_95_out, OP6, OP5, not_96_out, not_97_out, not_98_out);
  and and_17 (and_17_out, not_99_out, not_100_out, F12, OP6, OP5, not_101_out, not_102_out, not_103_out);
  and and_18 (and_18_out, not_104_out, not_105_out, not_106_out, OP6, OP5, not_107_out, not_108_out, OP2);
  and and_19 (and_19_out, not_109_out, not_110_out, not_111_out, not_112_out, not_113_out, not_114_out, OP5, OP4, not_115_out, not_116_out);
  and and_20 (and_20_out, F30, not_117_out, not_118_out, not_119_out, not_120_out, not_121_out, OP5, OP4, not_122_out, not_123_out);
  and and_21 (and_21_out, not_124_out, not_125_out, F14, F13, F12, not_126_out, OP5, OP4, not_127_out, not_128_out);
  and and_22 (and_22_out, not_129_out, not_130_out, not_131_out, F13, F12, not_132_out, OP5, OP4, not_133_out, not_134_out);
  and and_23 (and_23_out, not_135_out, not_136_out, not_137_out, not_138_out, not_139_out, OP4, not_140_out, not_141_out);
  and and_24 (and_24_out, F14, F13, F12, not_142_out, not_143_out, OP4, not_144_out, not_145_out);
  and and_25 (and_25_out, not_146_out, not_147_out, not_148_out, OP6, OP5, not_149_out, not_150_out, not_151_out);
  and and_26 (and_26_out, not_152_out, not_153_out, F12, OP6, OP5, not_154_out, not_155_out, not_156_out);
  and and_27 (and_27_out, not_157_out, not_158_out, not_159_out, OP6, OP5, not_160_out, not_161_out, OP2);
  and and_28 (and_28_out, F14, F13, not_162_out, OP6, OP5, not_163_out, not_164_out, not_165_out);
  and and_29 (and_29_out, not_166_out, not_167_out, F14, F13, not_168_out, not_169_out, OP5, OP4, not_170_out, not_171_out);
  and and_30 (and_30_out, not_172_out, not_173_out, not_174_out, F13, not_175_out, not_176_out, OP5, OP4, not_177_out, not_178_out);
  and and_31 (and_31_out, not_179_out, not_180_out, not_181_out, F13, F12, not_182_out, OP5, OP4, not_183_out, not_184_out);
  and and_32 (and_32_out, F14, F13, not_185_out, not_186_out, not_187_out, OP4, not_188_out, not_189_out);
  and and_33 (and_33_out, F14, not_190_out, not_191_out, not_192_out, not_193_out, OP4, not_194_out, not_195_out);
  and and_34 (and_34_out, not_196_out, F13, not_197_out, not_198_out, not_199_out, OP4, not_200_out, not_201_out);
  and and_35 (and_35_out, not_202_out, not_203_out, F14, not_204_out, not_205_out, not_206_out, OP5, OP4, not_207_out, not_208_out);
  and and_36 (and_36_out, F14, F13, not_209_out, OP6, OP5, not_210_out, not_211_out, not_212_out);
  or or_1 (S0, and_1_out, and_2_out, and_3_out, and_4_out, and_5_out, and_6_out, and_7_out, and_8_out, and_9_out);
  or or_2 (S1, and_10_out, and_11_out, and_12_out, and_13_out, and_14_out, and_15_out, and_16_out, and_17_out, and_18_out);
  or or_3 (S2, and_19_out, and_20_out, and_21_out, and_22_out, and_23_out, and_24_out, and_25_out, and_26_out, and_27_out, and_28_out);
  or or_4 (S3, and_29_out, and_30_out, and_31_out, and_32_out, and_33_out, and_34_out, and_35_out, and_36_out);
endmodule

// 控制信号生成
module \控制信号自动生成  (
  input  OP2,
  input  OP3,
  input  OP4,
  input  OP5,
  input  OP6,
  input  F12,
  input  F13,
  input  F14,
  input  F25,
  input  F30,
  output MemToReg,
  output MemWrite,
  output ALU_SRC,
  output RegWrite,
  output ecall,
  output S_Type,
  output BEQ,
  output BNE,
  output JALR,
  output JAL,
  output XOR,
  output LUI,
  output LH,
  output BLTU,
  output RS1_USED,
  output RS2_USED
);

  wire and_1_out, and_2_out, and_4_out, and_5_out, and_6_out, and_7_out, and_8_out, and_9_out, and_10_out,
       and_11_out, and_12_out, and_13_out, and_14_out, and_15_out, and_16_out, and_17_out, and_18_out,
       and_19_out, and_20_out, and_21_out, and_22_out, and_33_out, and_34_out, and_35_out, and_36_out,
       and_37_out, and_38_out, and_39_out, and_40_out, and_41_out, and_42_out, and_43_out, and_44_out,
       and_45_out, and_46_out, and_47_out, and_48_out, and_49_out, and_50_out, and_51_out, and_52_out,
       and_53_out, and_54_out, and_55_out, and_56_out, and_57_out, and_58_out, and_59_out, and_60_out,
       and_61_out, and_62_out, and_63_out, and_64_out, and_65_out, not_1_out, not_2_out, not_3_out,
       not_4_out, not_5_out, not_6_out, not_7_out, not_8_out, not_9_out, not_10_out, not_11_out, not_12_out,
       not_13_out, not_14_out, not_15_out, not_16_out, not_17_out, not_18_out, not_19_out, not_20_out,
       not_21_out, not_22_out, not_23_out, not_24_out, not_25_out, not_26_out, not_27_out, not_28_out,
       not_29_out, not_30_out, not_31_out, not_32_out, not_33_out, not_34_out, not_35_out, not_36_out,
       not_37_out, not_38_out, not_39_out, not_40_out, not_41_out, not_42_out, not_43_out, not_44_out,
       not_45_out, not_46_out, not_47_out, not_48_out, not_49_out, not_50_out, not_51_out, not_52_out,
       not_53_out, not_54_out, not_55_out, not_56_out, not_57_out, not_58_out, not_59_out, not_60_out,
       not_61_out, not_62_out, not_63_out, not_64_out, not_65_out, not_66_out, not_67_out, not_68_out,
       not_69_out, not_70_out, not_71_out, not_72_out, not_73_out, not_74_out, not_75_out, not_76_out,
       not_77_out, not_78_out, not_79_out, not_80_out, not_81_out, not_82_out, not_83_out, not_84_out,
       not_85_out, not_86_out, not_87_out, not_88_out, not_89_out, not_90_out, not_91_out, not_92_out,
       not_93_out, not_94_out, not_95_out, not_96_out, not_97_out, not_98_out, not_99_out, not_100_out,
       not_101_out, not_102_out, not_103_out, not_104_out, not_105_out, not_106_out, not_107_out,
       not_108_out, not_109_out, not_110_out, not_111_out, not_112_out, not_113_out, not_114_out,
       not_115_out, not_116_out, not_117_out, not_118_out, not_119_out, not_120_out, not_121_out,
       not_122_out, not_123_out, not_124_out, not_125_out, not_126_out, not_127_out, not_128_out,
       not_129_out, not_130_out, not_131_out, not_132_out, not_133_out, not_134_out, not_135_out,
       not_136_out, not_137_out, not_138_out, not_139_out, not_140_out, not_141_out, not_142_out,
       not_143_out, not_144_out, not_145_out, not_146_out, not_147_out, not_148_out, not_149_out,
       not_150_out, not_151_out, not_152_out, not_153_out, not_154_out, not_155_out, not_156_out,
       not_157_out, not_158_out, not_159_out, not_160_out, not_161_out, not_162_out, not_163_out,
       not_164_out, not_165_out, not_166_out, not_167_out, not_168_out, not_169_out, not_170_out,
       not_171_out, not_172_out, not_173_out, not_174_out, not_175_out, not_176_out, not_177_out,
       not_178_out, not_179_out, not_180_out, not_181_out, not_182_out, not_183_out, not_184_out,
       not_185_out, not_186_out, not_187_out, not_188_out, not_189_out, not_190_out, not_191_out,
       not_192_out, not_193_out, not_194_out, not_195_out, not_196_out, not_197_out, not_198_out,
       not_199_out, not_200_out, not_201_out, not_202_out, not_203_out, not_204_out, not_205_out,
       not_206_out, not_207_out, not_208_out, not_209_out, not_210_out, not_211_out, not_212_out,
       not_213_out, not_214_out, not_215_out, not_216_out, not_217_out, not_218_out, not_219_out,
       not_220_out, not_221_out, not_222_out, not_223_out, not_224_out, not_225_out, not_226_out,
       not_227_out, not_228_out, not_229_out, not_230_out, not_231_out, not_232_out, not_233_out,
       not_234_out, not_235_out, not_236_out, not_237_out, not_238_out, not_239_out, not_240_out,
       not_241_out, not_242_out, not_243_out, not_244_out, not_245_out, not_246_out, not_247_out,
       not_248_out, not_249_out, not_250_out, not_251_out, not_252_out, not_253_out, not_254_out,
       not_255_out, not_256_out, not_257_out, not_258_out, not_259_out, not_260_out, not_261_out,
       not_262_out, not_263_out, not_264_out, not_265_out, not_266_out, not_267_out, not_268_out,
       not_269_out, not_270_out, not_271_out, not_272_out, not_273_out, not_274_out, not_275_out,
       not_276_out, not_277_out, not_278_out, not_279_out, not_280_out, not_281_out, not_282_out,
       not_283_out, not_284_out, not_285_out, not_286_out, not_287_out, not_288_out, not_289_out,
       not_290_out, not_291_out, not_292_out, not_293_out, not_294_out, not_295_out, not_296_out,
       not_297_out, not_298_out, not_299_out, not_300_out, not_301_out, not_302_out, not_303_out,
       not_304_out, not_305_out, not_306_out, not_307_out, not_308_out, not_309_out, not_310_out,
       not_311_out, not_312_out, not_313_out, not_314_out, not_315_out, not_316_out, not_317_out,
       not_318_out, not_319_out, not_320_out, not_321_out, not_322_out, not_323_out, not_324_out,
       not_325_out, not_326_out, not_327_out, not_328_out, not_329_out, not_330_out, not_331_out,
       not_332_out, not_333_out, not_334_out, not_335_out, not_336_out, not_337_out, not_338_out,
       not_339_out, not_340_out, not_341_out, not_342_out, not_343_out, not_344_out, not_345_out,
       not_346_out, not_347_out, not_348_out, not_349_out, not_350_out, not_351_out, not_352_out,
       not_353_out, not_354_out, not_355_out, not_356_out, not_357_out, not_358_out, not_359_out,
       not_360_out, not_361_out, not_362_out, not_363_out, not_364_out, not_365_out, not_366_out,
       not_367_out, not_368_out, not_369_out;

  not not_1 (not_1_out, OP2);
  not not_2 (not_2_out, OP3);
  not not_3 (not_3_out, OP4);
  not not_4 (not_4_out, OP5);
  not not_5 (not_5_out, OP6);
  not not_6 (not_6_out, F12);
  not not_7 (not_7_out, F14);
  not not_8 (not_8_out, OP2);
  not not_9 (not_9_out, OP3);
  not not_10 (not_10_out, OP4);
  not not_11 (not_11_out, OP5);
  not not_12 (not_12_out, OP6);
  not not_13 (not_13_out, F13);
  not not_14 (not_14_out, F14);
  not not_15 (not_15_out, OP2);
  not not_16 (not_16_out, OP3);
  not not_17 (not_17_out, OP4);
  not not_18 (not_18_out, OP6);
  not not_19 (not_19_out, F12);
  not not_20 (not_20_out, F14);
  not not_21 (not_21_out, OP2);
  not not_22 (not_22_out, OP3);
  not not_23 (not_23_out, OP4);
  not not_24 (not_24_out, OP6);
  not not_25 (not_25_out, F12);
  not not_26 (not_26_out, F14);
  not not_27 (not_27_out, OP2);
  not not_28 (not_28_out, OP3);
  not not_29 (not_29_out, OP4);
  not not_30 (not_30_out, OP5);
  not not_31 (not_31_out, OP6);
  not not_32 (not_32_out, F13);
  not not_33 (not_33_out, F14);
  not not_34 (not_34_out, OP2);
  not not_35 (not_35_out, OP3);
  not not_36 (not_36_out, OP5);
  not not_37 (not_37_out, OP6);
  not not_38 (not_38_out, F12);
  not not_39 (not_39_out, OP2);
  not not_40 (not_40_out, OP3);
  not not_41 (not_41_out, OP5);
  not not_42 (not_42_out, OP6);
  not not_43 (not_43_out, F13);
  not not_44 (not_44_out, F25);
  not not_45 (not_45_out, F30);
  not not_46 (not_46_out, OP2);
  not not_47 (not_47_out, OP3);
  not not_48 (not_48_out, OP5);
  not not_49 (not_49_out, OP6);
  not not_50 (not_50_out, F25);
  not not_51 (not_51_out, OP2);
  not not_52 (not_52_out, OP3);
  not not_53 (not_53_out, OP5);
  not not_54 (not_54_out, OP6);
  not not_55 (not_55_out, OP3);
  not not_56 (not_56_out, OP4);
  not not_57 (not_57_out, F12);
  not not_58 (not_58_out, F13);
  not not_59 (not_59_out, F14);
  not not_60 (not_60_out, OP2);
  not not_61 (not_61_out, OP3);
  not not_62 (not_62_out, OP5);
  not not_63 (not_63_out, OP6);
  not not_64 (not_64_out, F12);
  not not_65 (not_65_out, F14);
  not not_66 (not_66_out, OP2);
  not not_67 (not_67_out, OP3);
  not not_68 (not_68_out, OP4);
  not not_69 (not_69_out, OP5);
  not not_70 (not_70_out, OP6);
  not not_71 (not_71_out, F13);
  not not_72 (not_72_out, F14);
  not not_73 (not_73_out, OP2);
  not not_74 (not_74_out, OP3);
  not not_75 (not_75_out, OP5);
  not not_76 (not_76_out, OP6);
  not not_77 (not_77_out, F12);
  not not_78 (not_78_out, OP2);
  not not_79 (not_79_out, OP3);
  not not_80 (not_80_out, OP5);
  not not_81 (not_81_out, OP6);
  not not_82 (not_82_out, F13);
  not not_83 (not_83_out, F25);
  not not_84 (not_84_out, F30);
  not not_85 (not_85_out, OP2);
  not not_86 (not_86_out, OP3);
  not not_87 (not_87_out, OP6);
  not not_88 (not_88_out, F12);
  not not_89 (not_89_out, F13);
  not not_90 (not_90_out, F14);
  not not_91 (not_91_out, F25);
  not not_92 (not_92_out, OP2);
  not not_93 (not_93_out, OP3);
  not not_94 (not_94_out, OP6);
  not not_95 (not_95_out, F12);
  not not_96 (not_96_out, F25);
  not not_97 (not_97_out, F30);
  not not_98 (not_98_out, OP2);
  not not_99 (not_99_out, OP3);
  not not_100 (not_100_out, OP5);
  not not_101 (not_101_out, OP6);
  not not_102 (not_102_out, F25);
  not not_103 (not_103_out, OP2);
  not not_104 (not_104_out, OP3);
  not not_105 (not_105_out, OP5);
  not not_106 (not_106_out, OP6);
  not not_107 (not_107_out, OP3);
  not not_108 (not_108_out, OP6);
  not not_109 (not_109_out, F25);
  not not_110 (not_110_out, F30);
  not not_111 (not_111_out, OP4);
  not not_112 (not_112_out, F12);
  not not_113 (not_113_out, F13);
  not not_114 (not_114_out, F14);
  not not_115 (not_115_out, OP3);
  not not_116 (not_116_out, OP6);
  not not_117 (not_117_out, OP4);
  not not_118 (not_118_out, OP2);
  not not_119 (not_119_out, OP3);
  not not_120 (not_120_out, F12);
  not not_121 (not_121_out, F13);
  not not_122 (not_122_out, F14);
  not not_123 (not_123_out, F25);
  not not_124 (not_124_out, F30);
  not not_125 (not_125_out, OP2);
  not not_126 (not_126_out, OP3);
  not not_127 (not_127_out, OP4);
  not not_128 (not_128_out, OP6);
  not not_129 (not_129_out, F12);
  not not_130 (not_130_out, F14);
  not not_131 (not_131_out, OP2);
  not not_132 (not_132_out, OP3);
  not not_133 (not_133_out, OP4);
  not not_134 (not_134_out, F12);
  not not_135 (not_135_out, F13);
  not not_136 (not_136_out, F14);
  not not_137 (not_137_out, OP2);
  not not_138 (not_138_out, OP3);
  not not_139 (not_139_out, OP4);
  not not_140 (not_140_out, F13);
  not not_141 (not_141_out, F14);
  not not_142 (not_142_out, OP3);
  not not_143 (not_143_out, OP4);
  not not_144 (not_144_out, F12);
  not not_145 (not_145_out, F13);
  not not_146 (not_146_out, F14);
  not not_147 (not_147_out, OP4);
  not not_148 (not_148_out, OP2);
  not not_149 (not_149_out, OP3);
  not not_150 (not_150_out, OP6);
  not not_151 (not_151_out, F12);
  not not_152 (not_152_out, F13);
  not not_153 (not_153_out, F25);
  not not_154 (not_154_out, F30);
  not not_155 (not_155_out, OP3);
  not not_156 (not_156_out, OP6);
  not not_157 (not_157_out, OP2);
  not not_158 (not_158_out, OP3);
  not not_159 (not_159_out, OP4);
  not not_160 (not_160_out, OP5);
  not not_161 (not_161_out, OP6);
  not not_162 (not_162_out, F13);
  not not_163 (not_163_out, F14);
  not not_164 (not_164_out, OP2);
  not not_165 (not_165_out, OP3);
  not not_166 (not_166_out, OP4);
  not not_167 (not_167_out, F12);
  not not_168 (not_168_out, F30);
  not not_169 (not_169_out, F25);
  not not_170 (not_170_out, F14);
  not not_171 (not_171_out, F13);
  not not_172 (not_172_out, F12);
  not not_173 (not_173_out, OP6);
  not not_174 (not_174_out, OP3);
  not not_175 (not_175_out, OP2);
  not not_176 (not_176_out, F25);
  not not_177 (not_177_out, F14);
  not not_178 (not_178_out, F13);
  not not_179 (not_179_out, F12);
  not not_180 (not_180_out, OP6);
  not not_181 (not_181_out, OP3);
  not not_182 (not_182_out, OP2);
  not not_183 (not_183_out, F30);
  not not_184 (not_184_out, F25);
  not not_185 (not_185_out, OP6);
  not not_186 (not_186_out, OP3);
  not not_187 (not_187_out, OP2);
  not not_188 (not_188_out, F30);
  not not_189 (not_189_out, F25);
  not not_190 (not_190_out, F12);
  not not_191 (not_191_out, OP6);
  not not_192 (not_192_out, OP3);
  not not_193 (not_193_out, OP2);
  not not_194 (not_194_out, F30);
  not not_195 (not_195_out, F25);
  not not_196 (not_196_out, F14);
  not not_197 (not_197_out, F12);
  not not_198 (not_198_out, OP6);
  not not_199 (not_199_out, OP3);
  not not_200 (not_200_out, OP2);
  not not_201 (not_201_out, F30);
  not not_202 (not_202_out, F25);
  not not_203 (not_203_out, F14);
  not not_204 (not_204_out, OP6);
  not not_205 (not_205_out, OP3);
  not not_206 (not_206_out, OP2);
  not not_207 (not_207_out, F14);
  not not_208 (not_208_out, F13);
  not not_209 (not_209_out, F12);
  not not_210 (not_210_out, OP6);
  not not_211 (not_211_out, OP5);
  not not_212 (not_212_out, OP3);
  not not_213 (not_213_out, OP2);
  not not_214 (not_214_out, OP6);
  not not_215 (not_215_out, OP5);
  not not_216 (not_216_out, OP3);
  not not_217 (not_217_out, OP2);
  not not_218 (not_218_out, F12);
  not not_219 (not_219_out, OP6);
  not not_220 (not_220_out, OP5);
  not not_221 (not_221_out, OP3);
  not not_222 (not_222_out, OP2);
  not not_223 (not_223_out, F13);
  not not_224 (not_224_out, F12);
  not not_225 (not_225_out, OP6);
  not not_226 (not_226_out, OP5);
  not not_227 (not_227_out, OP3);
  not not_228 (not_228_out, OP2);
  not not_229 (not_229_out, F14);
  not not_230 (not_230_out, F12);
  not not_231 (not_231_out, OP6);
  not not_232 (not_232_out, OP5);
  not not_233 (not_233_out, OP3);
  not not_234 (not_234_out, OP2);
  not not_235 (not_235_out, F30);
  not not_236 (not_236_out, F25);
  not not_237 (not_237_out, F14);
  not not_238 (not_238_out, F13);
  not not_239 (not_239_out, OP6);
  not not_240 (not_240_out, OP5);
  not not_241 (not_241_out, OP3);
  not not_242 (not_242_out, OP2);
  not not_243 (not_243_out, F30);
  not not_244 (not_244_out, F25);
  not not_245 (not_245_out, F13);
  not not_246 (not_246_out, OP6);
  not not_247 (not_247_out, OP5);
  not not_248 (not_248_out, OP3);
  not not_249 (not_249_out, OP2);
  not not_250 (not_250_out, F25);
  not not_251 (not_251_out, F13);
  not not_252 (not_252_out, OP6);
  not not_253 (not_253_out, OP5);
  not not_254 (not_254_out, OP3);
  not not_255 (not_255_out, OP2);
  not not_256 (not_256_out, F14);
  not not_257 (not_257_out, F12);
  not not_258 (not_258_out, OP6);
  not not_259 (not_259_out, OP5);
  not not_260 (not_260_out, OP4);
  not not_261 (not_261_out, OP3);
  not not_262 (not_262_out, OP2);
  not not_263 (not_263_out, F14);
  not not_264 (not_264_out, F12);
  not not_265 (not_265_out, OP6);
  not not_266 (not_266_out, OP4);
  not not_267 (not_267_out, OP3);
  not not_268 (not_268_out, OP2);
  not not_269 (not_269_out, F14);
  not not_270 (not_270_out, F13);
  not not_271 (not_271_out, F12);
  not not_272 (not_272_out, OP4);
  not not_273 (not_273_out, OP3);
  not not_274 (not_274_out, OP2);
  not not_275 (not_275_out, F14);
  not not_276 (not_276_out, F13);
  not not_277 (not_277_out, OP4);
  not not_278 (not_278_out, OP3);
  not not_279 (not_279_out, OP2);
  not not_280 (not_280_out, F14);
  not not_281 (not_281_out, F13);
  not not_282 (not_282_out, F12);
  not not_283 (not_283_out, OP4);
  not not_284 (not_284_out, OP3);
  not not_285 (not_285_out, F30);
  not not_286 (not_286_out, F25);
  not not_287 (not_287_out, F13);
  not not_288 (not_288_out, F12);
  not not_289 (not_289_out, OP6);
  not not_290 (not_290_out, OP3);
  not not_291 (not_291_out, OP2);
  not not_292 (not_292_out, F14);
  not not_293 (not_293_out, F13);
  not not_294 (not_294_out, OP6);
  not not_295 (not_295_out, OP5);
  not not_296 (not_296_out, OP4);
  not not_297 (not_297_out, OP3);
  not not_298 (not_298_out, OP2);
  not not_299 (not_299_out, F12);
  not not_300 (not_300_out, OP4);
  not not_301 (not_301_out, OP3);
  not not_302 (not_302_out, OP2);
  not not_303 (not_303_out, F30);
  not not_304 (not_304_out, F25);
  not not_305 (not_305_out, F14);
  not not_306 (not_306_out, F13);
  not not_307 (not_307_out, F12);
  not not_308 (not_308_out, OP6);
  not not_309 (not_309_out, OP3);
  not not_310 (not_310_out, OP2);
  not not_311 (not_311_out, F25);
  not not_312 (not_312_out, F14);
  not not_313 (not_313_out, F13);
  not not_314 (not_314_out, F12);
  not not_315 (not_315_out, OP6);
  not not_316 (not_316_out, OP3);
  not not_317 (not_317_out, OP2);
  not not_318 (not_318_out, F30);
  not not_319 (not_319_out, F25);
  not not_320 (not_320_out, OP6);
  not not_321 (not_321_out, OP3);
  not not_322 (not_322_out, OP2);
  not not_323 (not_323_out, F30);
  not not_324 (not_324_out, F25);
  not not_325 (not_325_out, F12);
  not not_326 (not_326_out, OP6);
  not not_327 (not_327_out, OP3);
  not not_328 (not_328_out, OP2);
  not not_329 (not_329_out, F30);
  not not_330 (not_330_out, F25);
  not not_331 (not_331_out, F14);
  not not_332 (not_332_out, F12);
  not not_333 (not_333_out, OP6);
  not not_334 (not_334_out, OP3);
  not not_335 (not_335_out, OP2);
  not not_336 (not_336_out, F30);
  not not_337 (not_337_out, F25);
  not not_338 (not_338_out, F14);
  not not_339 (not_339_out, OP6);
  not not_340 (not_340_out, OP3);
  not not_341 (not_341_out, OP2);
  not not_342 (not_342_out, F14);
  not not_343 (not_343_out, F12);
  not not_344 (not_344_out, OP6);
  not not_345 (not_345_out, OP4);
  not not_346 (not_346_out, OP3);
  not not_347 (not_347_out, OP2);
  not not_348 (not_348_out, F14);
  not not_349 (not_349_out, F13);
  not not_350 (not_350_out, F12);
  not not_351 (not_351_out, OP4);
  not not_352 (not_352_out, OP3);
  not not_353 (not_353_out, OP2);
  not not_354 (not_354_out, F14);
  not not_355 (not_355_out, F13);
  not not_356 (not_356_out, OP4);
  not not_357 (not_357_out, OP3);
  not not_358 (not_358_out, OP2);
  not not_359 (not_359_out, F30);
  not not_360 (not_360_out, F25);
  not not_361 (not_361_out, F13);
  not not_362 (not_362_out, F12);
  not not_363 (not_363_out, OP6);
  not not_364 (not_364_out, OP3);
  not not_365 (not_365_out, OP2);
  not not_366 (not_366_out, F12);
  not not_367 (not_367_out, OP4);
  not not_368 (not_368_out, OP3);
  not not_369 (not_369_out, OP2);
  and and_1 (and_1_out, not_1_out, not_2_out, not_3_out, not_4_out, not_5_out, not_6_out, F13, not_7_out);
  and and_2 (and_2_out, not_8_out, not_9_out, not_10_out, not_11_out, not_12_out, F12, not_13_out, not_14_out);
  and and_3 (MemWrite, not_15_out, not_16_out, not_17_out, OP5, not_18_out, not_19_out, F13, not_20_out);
  and and_4 (and_4_out, not_21_out, not_22_out, not_23_out, not_24_out, not_25_out, F13, not_26_out);
  and and_5 (and_5_out, not_27_out, not_28_out, not_29_out, not_30_out, not_31_out, F12, not_32_out, not_33_out);
  and and_6 (and_6_out, not_34_out, not_35_out, OP4, not_36_out, not_37_out, not_38_out);
  and and_7 (and_7_out, not_39_out, not_40_out, OP4, not_41_out, not_42_out, not_43_out, not_44_out, not_45_out);
  and and_8 (and_8_out, not_46_out, not_47_out, OP4, not_48_out, not_49_out, F14, not_50_out);
  and and_9 (and_9_out, not_51_out, not_52_out, OP4, not_53_out, not_54_out, F13, F14);
  and and_10 (and_10_out, OP2, not_55_out, not_56_out, OP5, OP6, not_57_out, not_58_out, not_59_out);
  and and_11 (and_11_out, not_60_out, not_61_out, not_62_out, not_63_out, not_64_out, F13, not_65_out);
  and and_12 (and_12_out, not_66_out, not_67_out, not_68_out, not_69_out, not_70_out, F12, not_71_out, not_72_out);
  and and_13 (and_13_out, not_73_out, not_74_out, OP4, not_75_out, not_76_out, not_77_out);
  and and_14 (and_14_out, not_78_out, not_79_out, OP4, not_80_out, not_81_out, not_82_out, not_83_out, not_84_out);
  and and_15 (and_15_out, not_85_out, not_86_out, OP4, not_87_out, not_88_out, not_89_out, not_90_out, not_91_out);
  and and_16 (and_16_out, not_92_out, not_93_out, OP4, not_94_out, not_95_out, not_96_out, not_97_out);
  and and_17 (and_17_out, not_98_out, not_99_out, OP4, not_100_out, not_101_out, F14, not_102_out);
  and and_18 (and_18_out, not_103_out, not_104_out, OP4, not_105_out, not_106_out, F13, F14);
  and and_19 (and_19_out, not_107_out, OP4, OP5, not_108_out, F13, not_109_out, not_110_out);
  and and_20 (and_20_out, OP2, not_111_out, OP5, OP6, not_112_out, not_113_out, not_114_out);
  and and_21 (and_21_out, OP2, not_115_out, OP4, OP5, not_116_out);
  and and_22 (and_22_out, OP2, OP3, not_117_out, OP5, OP6);
  and and_23 (ecall, not_118_out, not_119_out, OP4, OP5, OP6, not_120_out, not_121_out, not_122_out, not_123_out, not_124_out);
  and and_24 (S_Type, not_125_out, not_126_out, not_127_out, OP5, not_128_out, not_129_out, F13, not_130_out);
  and and_25 (BEQ, not_131_out, not_132_out, not_133_out, OP5, OP6, not_134_out, not_135_out, not_136_out);
  and and_26 (BNE, not_137_out, not_138_out, not_139_out, OP5, OP6, F12, not_140_out, not_141_out);
  and and_27 (JALR, OP2, not_142_out, not_143_out, OP5, OP6, not_144_out, not_145_out, not_146_out);
  and and_28 (JAL, OP2, OP3, not_147_out, OP5, OP6);
  and and_29 (XOR, not_148_out, not_149_out, OP4, OP5, not_150_out, not_151_out, not_152_out, F14, not_153_out, not_154_out);
  and and_30 (LUI, OP2, not_155_out, OP4, OP5, not_156_out);
  and and_31 (LH, not_157_out, not_158_out, not_159_out, not_160_out, not_161_out, F12, not_162_out, not_163_out);
  and and_32 (BLTU, not_164_out, not_165_out, not_166_out, OP5, OP6, not_167_out, F13, F14);
  and and_33 (and_33_out, not_168_out, not_169_out, not_170_out, not_171_out, not_172_out, not_173_out, OP5, OP4, not_174_out, not_175_out);
  and and_34 (and_34_out, F30, not_176_out, not_177_out, not_178_out, not_179_out, not_180_out, OP5, OP4, not_181_out, not_182_out);
  and and_35 (and_35_out, not_183_out, not_184_out, F14, F13, F12, not_185_out, OP5, OP4, not_186_out, not_187_out);
  and and_36 (and_36_out, not_188_out, not_189_out, F14, F13, not_190_out, not_191_out, OP5, OP4, not_192_out, not_193_out);
  and and_37 (and_37_out, not_194_out, not_195_out, not_196_out, F13, not_197_out, not_198_out, OP5, OP4, not_199_out, not_200_out);
  and and_38 (and_38_out, not_201_out, not_202_out, not_203_out, F13, F12, not_204_out, OP5, OP4, not_205_out, not_206_out);
  and and_39 (and_39_out, not_207_out, not_208_out, not_209_out, not_210_out, not_211_out, OP4, not_212_out, not_213_out);
  and and_40 (and_40_out, F14, F13, F12, not_214_out, not_215_out, OP4, not_216_out, not_217_out);
  and and_41 (and_41_out, F14, F13, not_218_out, not_219_out, not_220_out, OP4, not_221_out, not_222_out);
  and and_42 (and_42_out, F14, not_223_out, not_224_out, not_225_out, not_226_out, OP4, not_227_out, not_228_out);
  and and_43 (and_43_out, not_229_out, F13, not_230_out, not_231_out, not_232_out, OP4, not_233_out, not_234_out);
  and and_44 (and_44_out, not_235_out, not_236_out, not_237_out, not_238_out, F12, not_239_out, not_240_out, OP4, not_241_out, not_242_out);
  and and_45 (and_45_out, not_243_out, not_244_out, F14, not_245_out, F12, not_246_out, not_247_out, OP4, not_248_out, not_249_out);
  and and_46 (and_46_out, F30, not_250_out, F14, not_251_out, F12, not_252_out, not_253_out, OP4, not_254_out, not_255_out);
  and and_47 (and_47_out, not_256_out, F13, not_257_out, not_258_out, not_259_out, not_260_out, not_261_out, not_262_out);
  and and_48 (and_48_out, not_263_out, F13, not_264_out, not_265_out, OP5, not_266_out, not_267_out, not_268_out);
  and and_49 (and_49_out, not_269_out, not_270_out, not_271_out, OP6, OP5, not_272_out, not_273_out, not_274_out);
  and and_50 (and_50_out, not_275_out, not_276_out, F12, OP6, OP5, not_277_out, not_278_out, not_279_out);
  and and_51 (and_51_out, not_280_out, not_281_out, not_282_out, OP6, OP5, not_283_out, not_284_out, OP2);
  and and_52 (and_52_out, not_285_out, not_286_out, F14, not_287_out, not_288_out, not_289_out, OP5, OP4, not_290_out, not_291_out);
  and and_53 (and_53_out, not_292_out, not_293_out, F12, not_294_out, not_295_out, not_296_out, not_297_out, not_298_out);
  and and_54 (and_54_out, F14, F13, not_299_out, OP6, OP5, not_300_out, not_301_out, not_302_out);
  and and_55 (and_55_out, not_303_out, not_304_out, not_305_out, not_306_out, not_307_out, not_308_out, OP5, OP4, not_309_out, not_310_out);
  and and_56 (and_56_out, F30, not_311_out, not_312_out, not_313_out, not_314_out, not_315_out, OP5, OP4, not_316_out, not_317_out);
  and and_57 (and_57_out, not_318_out, not_319_out, F14, F13, F12, not_320_out, OP5, OP4, not_321_out, not_322_out);
  and and_58 (and_58_out, not_323_out, not_324_out, F14, F13, not_325_out, not_326_out, OP5, OP4, not_327_out, not_328_out);
  and and_59 (and_59_out, not_329_out, not_330_out, not_331_out, F13, not_332_out, not_333_out, OP5, OP4, not_334_out, not_335_out);
  and and_60 (and_60_out, not_336_out, not_337_out, not_338_out, F13, F12, not_339_out, OP5, OP4, not_340_out, not_341_out);
  and and_61 (and_61_out, not_342_out, F13, not_343_out, not_344_out, OP5, not_345_out, not_346_out, not_347_out);
  and and_62 (and_62_out, not_348_out, not_349_out, not_350_out, OP6, OP5, not_351_out, not_352_out, not_353_out);
  and and_63 (and_63_out, not_354_out, not_355_out, F12, OP6, OP5, not_356_out, not_357_out, not_358_out);
  and and_64 (and_64_out, not_359_out, not_360_out, F14, not_361_out, not_362_out, not_363_out, OP5, OP4, not_364_out, not_365_out);
  and and_65 (and_65_out, F14, F13, not_366_out, OP6, OP5, not_367_out, not_368_out, not_369_out);
  or or_1 (MemToReg, and_1_out, and_2_out);
  or or_2 (ALU_SRC, and_4_out, and_5_out, and_6_out, and_7_out, and_8_out, and_9_out, and_10_out);
  or or_3 (RegWrite, and_11_out, and_12_out, and_13_out, and_14_out, and_15_out, and_16_out, and_17_out, and_18_out, and_19_out, and_20_out, and_21_out, and_22_out);
  or or_4 (RS2_USED, and_55_out, and_56_out, and_57_out, and_58_out, and_59_out, and_60_out, and_61_out, and_62_out, and_63_out, and_64_out, and_65_out);
  or or_5 (RS1_USED, and_33_out, and_34_out, and_35_out, and_36_out, and_37_out, and_38_out, and_39_out, and_40_out, and_41_out, and_42_out, and_43_out, and_44_out, and_45_out, and_46_out, and_47_out, and_48_out, and_49_out, and_50_out, and_51_out, and_52_out, and_53_out, and_54_out);
endmodule

// ALU
module ALU (
  input  [31:0] X,
  input  [31:0] Y,
  input  [3:0] AluOP,
  output out_4,
  output Equal,
  output out_6,
  output [31:0] Result,
  output [31:0] Result_2
);

  wire [0:0] comparator_1_lt, comparator_2_lt;
  wire [31:0] adder_1_out, AND_out, divider_1_out, divider_1_rem, multiplier_1_cout, multiplier_1_out,
       NOR_out, OR_out, shifter_1_out, shifter_2_out, shifter_3_out, subtractor_1_out, XOR_out;

  assign AND_out = X & Y;  // AND_Gate AND, 32 bits wide
  assign OR_out = X | Y;  // OR_Gate OR, 32 bits wide
  Shifter #(.width(32), .shift("ll")) shifter_1 (.in(X), .\dist (Y[4:0]), .out(shifter_1_out));
  Shifter #(.width(32), .shift("ar")) shifter_2 (.in(X), .\dist (Y[4:0]), .out(shifter_2_out));
  Shifter #(.width(32), .shift("lr")) shifter_3 (.in(X), .\dist (Y[4:0]), .out(shifter_3_out));
  Multiplier #(.width(32)) multiplier_1 (.a(X), .b(Y), .out(multiplier_1_out), .cout(multiplier_1_cout));  // open: cin
  Divider #(.width(32)) divider_1 (.a(X), .b(Y), .out(divider_1_out), .rem(divider_1_rem));  // open: upper
  Adder #(.width(32)) adder_1 (.a(X), .b(Y), .out(adder_1_out));  // open: cin, cout
  Subtractor #(.width(32)) subtractor_1 (.a(X), .b(Y), .out(subtractor_1_out));  // open: bin, bout
  assign XOR_out = X ^ Y;  // XOR_Gate XOR, 32 bits wide
  assign NOR_out = ~(X | Y);  // NOR_Gate NOR, 32 bits wide
  Comparator #(.width(32), .mode("twosComplement")) comparator_1 (
    .a(X), .b(Y), .eq(Equal), .lt(comparator_1_lt[0]));  // open: gt
  Comparator #(.width(32), .mode("unsigned")) comparator_2 (.a(X), .b(Y), .lt(comparator_2_lt[0]));  // open: gt, eq
  Multiplexer #(.select(4), .width(32), .disabled("Z"), .enable("false")) multiplexer_1 (
    .in0(shifter_1_out), .in1(shifter_2_out), .in2(shifter_3_out), .in3(multiplier_1_out),
    .in4(divider_1_out), .in5(adder_1_out), .in6(subtractor_1_out), .in7(AND_out), .in8(OR_out),
    .in9(XOR_out), .in10(NOR_out), .in11({{31{1'b0}}, comparator_1_lt[0]}),
    .in12({{31{1'b0}}, comparator_2_lt[0]}), .in13({32{1'b0}}), .in14({32{1'b0}}), .in15({32{1'b0}}),
    .out(Result), .sel(AluOP));
  Multiplexer #(.select(4), .width(32), .disabled("Z"), .enable("false")) multiplexer_2 (
    .in0({32{1'b0}}), .in1({32{1'b0}}), .in2({32{1'b0}}), .in3(multiplier_1_cout), .in4(divider_1_rem),
    .in5({32{1'b0}}), .in6({32{1'b0}}), .in7({32{1'b0}}), .in8({32{1'b0}}), .in9({32{1'b0}}),
    .in10({32{1'b0}}), .in11({32{1'b0}}), .in12({32{1'b0}}), .in13({32{1'b0}}), .in14({32{1'b0}}),
    .in15({32{1'b0}}), .out(Result_2), .sel(AluOP));
  Multiplexer #(.select(4), .width(1), .disabled("Z"), .enable("false")) multiplexer_3 (
    .in0(1'b0), .in1(1'b0), .in2(1'b0), .in3(1'b0), .in4(1'b0), .in5(1'b0), .in6(1'b0), .in7(1'b0),
    .in8(1'b0), .in9(1'b0), .in10(1'b0), .in11(comparator_1_lt[0]), .in12(comparator_2_lt[0]), .in13(1'b0),
    .in14(1'b0), .in15(1'b0), .out(out_6), .sel(AluOP));
  not not_1 (out_4, out_6);

  // Other names for the same wires on the sheet: Result2[31:0] = Result_2; S[3:0] = AluOP; tunnel = out_6;
  //   tunnel_t = out_4

  // Notes on the sheet:
  //   不要改变此引脚区域内容，也不要改变ALU封装形式
  //   输入引脚
  //   输出引脚
endmodule

module Regifile (
  input  [31:0] Din,
  input  Clk,
  input  WE,
  input  [4:0] R1_num,
  input  [4:0] W_num,
  input  [4:0] R2_num,
  output [31:0] R1,
  output [31:0] R2
);

  // RegisterFile registerfile_1: pin names not known; wires that end beside it: Din, Clk, WE, W_num, R1_num, R2_num, R1, R2
endmodule

module \理想流水线  (
  output RegWrite,
  output MemWrite,
  output [31:0] IF_PC,
  output [31:0] ID_PC,
  output [31:0] EX_PC,
  output [31:0] M_PC,
  output [31:0] WB_PC,
  output [31:0] RDin,
  output [31:0] MDin,
  output [31:0] LedData
);

  wire alu_1_equal, and_1_out, and_2_out, and_3_out, CLK, clock_1_out, clock_2_out, comparator_1_eq,
       comparator_1_lt, d_ff_1_q, ecall, EX_ecall, EX_halt, EX_MEM_halt_2, EX_MEM_jal_2, EX_MEM_jalr_2,
       EX_MEM_memtoreg_2, EX_MEM_regwrite_2, Go, halt, ID_EX_alusrcb_2, ID_EX_beq_2, ID_EX_bltu_2,
       ID_EX_bne_2, ID_EX_jal_2, ID_EX_memtoreg_2, ID_EX_memwrite_2, ID_EX_regwrite_2, IR1, IR2, IR3,
       MEM_WB_halt_2, MEM_WB_jal_2, MEM_WB_jalr_2, nand_1_out, not_1_out, not_2_out, RST, W1, W2, W3,
       \单周期硬布线控制器_1_alu_src , \单周期硬布线控制器_1_beq , \单周期硬布线控制器_1_bltu , \单周期硬布线控制器_1_bne , \单周期硬布线控制器_1_jal ,
       \单周期硬布线控制器_1_jalr , \单周期硬布线控制器_1_lh , \单周期硬布线控制器_1_lui , \单周期硬布线控制器_1_memtoreg ,
       \单周期硬布线控制器_1_memwrite , \单周期硬布线控制器_1_regwrite , \单周期硬布线控制器_1_s_type ;
  wire [1:0] ID_EX_jalr_2, MEM_WB_memtoreg;
  wire [3:0] ID_EX_aluop_2, \单周期硬布线控制器_1_alu_op ;
  wire [4:0] EX_MEM_rd_2, ID_EX_rd_2, multiplexer_2_out, multiplexer_3_out, WB_rd;
  wire [12:0] CNT_num;
  wire [15:0] \LoadUse次数 , \总周期数 , \插入气泡数 , \无条件分支数 , \条件分支成功数 ;
  wire [31:0] ALU_addr, bit_extender_1_out, bit_extender_2_out, bit_extender_3_out, bit_extender_4_out,
       branch_addr, EX_IR, EX_MEM_pc_4_2, EX_MEM_result_2, ID_EX_imm_1_2, ID_EX_imm_2_2, ID_EX_pc_4_2,
       ID_EX_r1_2, ID_EX_r2_2, ID_IR, IF_ID_pc_4_2, IF_IR, MEM_IR, MEM_WB_aluresult_2, MEM_WB_pc_4_2,
       MEM_WB_readdata_2, multiplexer_1_out, multiplexer_4_out, multiplexer_5_out, multiplexer_6_out, PC_4,
       ram_1_data, regifile_1_r1, regifile_1_r2, shifter_1_out, WB_IR;

  Button \u_总复位  (.out(RST));
  Button _1 (.out(IR1));
  Button _2 (.out(IR2));
  Button _3 (.out(IR3));
  // Probe on \总周期数 
  // Probe on \总周期数 
  Button \u_继续运行  (.out(Go));
  LED #(.active("true")) led_1 (.in(W1));
  LED #(.active("true")) led_2 (.in(W2));
  LED #(.active("true")) led_3 (.in(W3));
  Hex_Digit_Display hex_digit_display_1 (.value(LedData[31:28]));  // open: dp
  // Probe on IF_PC[19:0]
  // RiscV_Probe riscv_probe_1: pin names not known; wires that end beside it: IF_IR
  Multiplexer #(.select(2), .width(32), .disabled("Z"), .enable("false")) multiplexer_1 (
    .in0(PC_4), .in1(ALU_addr), .in2(branch_addr), .out(multiplexer_1_out), .sel(ID_EX_jalr_2));  // open: in3
  Register #(.width(32), .trigger("rising"), .Select("low")) PC (
    .D(multiplexer_1_out), .en(not_1_out), .Q(IF_PC), .clk(CLK), .clr(RST));
  not not_1 (not_1_out, halt);
  Hex_Digit_Display hex_digit_display_2 (.value(LedData[27:24]));  // open: dp
  Hex_Digit_Display hex_digit_display_3 (.value(LedData[23:20]));  // open: dp
  // Probe on ID_PC[19:0]
  // RiscV_Probe riscv_probe_2: pin names not known; wires that end beside it: ID_IR
  Hex_Digit_Display hex_digit_display_4 (.value(LedData[15:12]));  // open: dp
  Hex_Digit_Display hex_digit_display_5 (.value(LedData[19:16]));  // open: dp
  // RiscV_Probe riscv_probe_3: pin names not known; wires that end beside it: IF_IR, RST
  Adder #(.width(32)) adder_1 (.a(IF_PC), .b(32'h4), .out(PC_4));  // open: cin, cout
  Hex_Digit_Display hex_digit_display_6 (.value(LedData[7:4]));  // open: dp
  Hex_Digit_Display hex_digit_display_7 (.value(LedData[11:8]));  // open: dp
  Clock #(.highDuration(1), .lowDuration(1)) clock_1 (.out(clock_1_out));
  // Probe on EX_PC[19:0]
  // RiscV_Probe riscv_probe_4: pin names not known; wires that end beside it: clock_1_out, EX_IR, CLK
  ROM #(.addrWidth(10), .dataWidth(32), .Select("high")) \u_指令存储器  (.addr(IF_PC[11:2]), .data(IF_IR));
  Hex_Digit_Display hex_digit_display_8 (.value(LedData[3:0]));  // open: dp
  IF_ID IF_ID (
    .IR(IF_IR), .PC(IF_PC), .PC_4(PC_4), .IR_2(ID_IR), .PC_2(ID_PC), .PC_4_2(IF_ID_pc_4_2), .reset(RST),
    .en(1'b1), .clk(CLK));  // open: BranchTaken
  // Probe on \总周期数 
  // Probe on M_PC[19:0]
  // RiscV_Probe riscv_probe_5: pin names not known; wires that end beside it: MEM_IR
  // Probe on \总周期数 
  // Probe on \无条件分支数 
  // Probe on \条件分支成功数 
  // Probe on \插入气泡数 
  // Probe on \LoadUse次数 
  \单周期硬布线控制器  \u_单周期硬布线控制器_1  (
    .Funct({ID_IR[30], ID_IR[25], ID_IR[14:12]}), .OP(ID_IR[6:2]), .ALU_OP(\单周期硬布线控制器_1_alu_op ),
    .MemToReg(\单周期硬布线控制器_1_memtoreg ), .MemWrite(\单周期硬布线控制器_1_memwrite ), .ALU_SRC(\单周期硬布线控制器_1_alu_src ),
    .RegWrite(\单周期硬布线控制器_1_regwrite ), .ecall(ecall), .S_type(\单周期硬布线控制器_1_s_type ),
    .Jalr(\单周期硬布线控制器_1_jalr ), .Beq(\单周期硬布线控制器_1_beq ), .JAL(\单周期硬布线控制器_1_jal ), .Bne(\单周期硬布线控制器_1_bne ),
    .BLTU(\单周期硬布线控制器_1_bltu ), .LUI(\单周期硬布线控制器_1_lui ), .LH(\单周期硬布线控制器_1_lh ), .in_3(ID_IR[21]));  // open: XOR, RS1_USED, RS2_USED, uret
  assign bit_extender_1_out = {{20{ID_IR[31]}}, ID_IR[31:20]};  // Bit_Extender bit_extender_1
  assign bit_extender_2_out = {{20{ID_IR[31]}}, {ID_IR[31:25], ID_IR[11:7]}};  // Bit_Extender bit_extender_2
  assign bit_extender_3_out = {{20{ID_IR[31]}}, {ID_IR[31], ID_IR[7], ID_IR[30:25], ID_IR[11:8]}};  // Bit_Extender bit_extender_3
  assign bit_extender_4_out = {{12{ID_IR[31]}}, {ID_IR[31], ID_IR[19:12], ID_IR[20], ID_IR[30:21]}};  // Bit_Extender bit_extender_4
  // Probe on IF_PC[11:0]
  // Probe on WB_PC[19:0]
  // RiscV_Probe riscv_probe_6: pin names not known; wires that end beside it: WB_IR
  Multiplexer #(.select(1), .width(5), .disabled("Z"), .enable("false")) multiplexer_2 (
    .in0(ID_IR[19:15]), .in1(5'b10001), .out(multiplexer_2_out), .sel(ecall));
  Multiplexer #(.select(1), .width(5), .disabled("Z"), .enable("false")) multiplexer_3 (
    .in0(ID_IR[24:20]), .in1(5'b01010), .out(multiplexer_3_out), .sel(ecall));
  Multiplexer #(.select(1), .width(32), .disabled("Z"), .enable("false")) multiplexer_4 (
    .in0(bit_extender_1_out), .in1(bit_extender_2_out), .out(multiplexer_4_out), .sel(\单周期硬布线控制器_1_s_type ));
  Multiplexer #(.select(1), .width(32), .disabled("Z"), .enable("false")) multiplexer_5 (
    .in0(bit_extender_3_out), .in1(bit_extender_4_out), .out(multiplexer_5_out), .sel(\单周期硬布线控制器_1_jal ));
  // Probe on ID_PC[11:0]
  // Probe on EX_PC[11:0]
  // Probe on M_PC[11:0]
  D_Flip_Flop #(.trigger("high"), .Pre_Clr_Positions("LEGACY"), .NegatePresetClear("false"), .enable("true"), .NewFFLayout("false")) d_ff_1 (.Q(d_ff_1_q));  // open: clk, D, Qn, preset, en, reset
  // Probe on 13'hc
  Regifile regifile_1 (
    .Din(RDin), .Clk(CLK), .R1(regifile_1_r1), .R2(regifile_1_r2), .WE(RegWrite), .W_num(WB_rd),
    .R1_num(multiplexer_2_out), .R2_num(multiplexer_3_out));
  // Probe on WB_PC[11:0]
  Comparator #(.width(13), .mode("twosComplement")) comparator_1 (
    .a(CNT_num), .b(13'hc), .eq(comparator_1_eq), .lt(comparator_1_lt));  // open: gt
  Clock #(.highDuration(1), .lowDuration(1)) clock_2 (.out(clock_2_out));
  ID_EX ID_EX (
    .Beq(\单周期硬布线控制器_1_beq ), .Bne(\单周期硬布线控制器_1_bne ), .MemToReg(\单周期硬布线控制器_1_memtoreg ),
    .MemWrite(\单周期硬布线控制器_1_memwrite ), .AluSrcB(\单周期硬布线控制器_1_alu_src ), .RegWrite(\单周期硬布线控制器_1_regwrite ),
    .SType(\单周期硬布线控制器_1_s_type ), .ecall(ecall), .Jal(\单周期硬布线控制器_1_jal ), .Jalr(\单周期硬布线控制器_1_jalr ),
    .LUI(\单周期硬布线控制器_1_lui ), .LH(\单周期硬布线控制器_1_lh ), .BLTU(\单周期硬布线控制器_1_bltu ), .AluOP(\单周期硬布线控制器_1_alu_op ),
    .rd(ID_IR[11:7]), .R1(regifile_1_r1), .R2(regifile_1_r2), .imm_1(multiplexer_4_out),
    .imm_2(multiplexer_5_out), .PC(ID_PC), .PC_4(IF_ID_pc_4_2), .IR(ID_IR), .Beq_2(ID_EX_beq_2),
    .Bne_2(ID_EX_bne_2), .MemToReg_2(ID_EX_memtoreg_2), .MemWrite_2(ID_EX_memwrite_2),
    .AluSrcB_2(ID_EX_alusrcb_2), .RegWrite_2(ID_EX_regwrite_2), .ecall_2(EX_ecall), .Jal_2(ID_EX_jal_2),
    .Jalr_2(ID_EX_jalr_2[0]), .BLTU_2(ID_EX_bltu_2), .AluOP_2(ID_EX_aluop_2), .rd_2(ID_EX_rd_2),
    .R1_2(ID_EX_r1_2), .R2_2(ID_EX_r2_2), .imm_1_2(ID_EX_imm_1_2), .imm_2_2(ID_EX_imm_2_2), .PC_2(EX_PC),
    .PC_4_2(ID_EX_pc_4_2), .IR_2(EX_IR), .reset(RST), .en(1'b1), .clk(CLK));  // open: RS1_Forward, RS2_Forward, SType_2, LUI_2, LH_2, RS1_Forward_2, RS2_Forward_2, flush
  nand nand_1 (nand_1_out, d_ff_1_q, comparator_1_eq);
  Counter #(.width(13), .max('h1fff), .ongoal("stay"), .trigger("rising"), .behavior("old")) counter_1 (
    .count(comparator_1_lt), .Q(CNT_num), .clk(clock_2_out));  // open: load, D, carry, clr, preset
  assign CLK = nand_1_out ? clock_2_out : 1'bz;  // Controlled_Buffer controlled_buffer_1
  Multiplexer #(.select(1), .width(32), .disabled("Z"), .enable("false")) multiplexer_6 (
    .in0(ID_EX_r2_2), .in1(ID_EX_imm_1_2), .out(multiplexer_6_out), .sel(ID_EX_alusrcb_2));
  Shifter #(.width(32), .shift("ll")) shifter_1 (.in(ID_EX_imm_2_2), .\dist (5'b00001), .out(shifter_1_out));
  Comparator #(.width(32), .mode("twosComplement")) comparator_2 (
    .a(ID_EX_r1_2), .b(32'ha), .eq(EX_halt));  // open: gt, lt
  not not_2 (not_2_out, EX_halt);
  Pull_Resistor #(.pull(1)) pull_resistor_1 (.node(CLK));
  and and_1 (and_1_out, ID_EX_beq_2, alu_1_equal);
  Adder #(.width(32)) adder_2 (.a(shifter_1_out), .b(EX_PC), .out(branch_addr));  // open: cin, cout
  and and_2 (and_2_out, not_2_out, EX_ecall);
  or or_1 (ID_EX_jalr_2[1], and_1_out, ID_EX_jal_2, and_3_out);
  and and_3 (and_3_out, ID_EX_bne_2, ~alu_1_equal);  // AND_Gate
  ALU alu_1 (
    .X(ID_EX_r1_2), .Y(multiplexer_6_out), .AluOP(ID_EX_aluop_2), .Equal(alu_1_equal), .Result(ALU_addr));  // open: Result_2, out_4, out_6
  Register #(.width(32), .trigger("rising"), .Select("low")) PC_2 (
    .D(ID_EX_r2_2), .en(and_2_out), .Q(LedData), .clk(CLK));  // open: clr
  EX_MEM EX_MEM (
    .JAL(ID_EX_jal_2), .Jalr(ID_EX_jalr_2[0]), .MemToReg(ID_EX_memtoreg_2), .MemWrite(ID_EX_memwrite_2),
    .RegWrite(ID_EX_regwrite_2), .halt(EX_halt), .rd(ID_EX_rd_2), .result(ALU_addr), .WriteData(ID_EX_r2_2),
    .IR(EX_IR), .PC(EX_PC), .PC_4(ID_EX_pc_4_2), .JAL_2(EX_MEM_jal_2), .Jalr_2(EX_MEM_jalr_2),
    .MemToReg_2(EX_MEM_memtoreg_2), .MemWrite_2(MemWrite), .RegWrite_2(EX_MEM_regwrite_2),
    .halt_2(EX_MEM_halt_2), .rd_2(EX_MEM_rd_2), .result_2(EX_MEM_result_2), .WriteData_2(MDin),
    .IR_2(MEM_IR), .PC_2(M_PC), .PC_4_2(EX_MEM_pc_4_2), .reset(RST), .en(1'b1), .clk(CLK));  // open: LH, LH_2
  RAM #(.addrWidth(10), .dataWidth(32), .bus("separate"), .Select("high")) ram_1 (
    .addr(EX_MEM_result_2[11:2]), .din(MDin), .data(ram_1_data), .str(MemWrite), .sel(1'b1), .clk(CLK),
    .ld(1'b1), .clr(RST));
  MEM_WB MEM_WB (
    .Jal(EX_MEM_jal_2), .Jalr(EX_MEM_jalr_2), .MenToReg(EX_MEM_memtoreg_2), .RegWrite(EX_MEM_regwrite_2),
    .halt(EX_MEM_halt_2), .rd(EX_MEM_rd_2), .ALUResult(EX_MEM_result_2), .ReadData(ram_1_data), .IR(MEM_IR),
    .PC(M_PC), .PC_4(EX_MEM_pc_4_2), .Jal_2(MEM_WB_jal_2), .Jalr_2(MEM_WB_jalr_2),
    .MemToReg(MEM_WB_memtoreg[0]), .RegWrite_2(RegWrite), .halt_2(MEM_WB_halt_2), .rd_2(WB_rd),
    .ALUResult_2(MEM_WB_aluresult_2), .ReadData_2(MEM_WB_readdata_2), .IR_2(WB_IR), .PC_2(WB_PC),
    .PC_4_2(MEM_WB_pc_4_2), .reset(RST), .en(1'b1), .clk(CLK));
  or or_2 (MEM_WB_memtoreg[1], MEM_WB_jal_2, MEM_WB_jalr_2);
  D_Flip_Flop #(.trigger("rising"), .Pre_Clr_Positions("ABOVE_BELOW"), .NegatePresetClear("false"), .enable("true"), .NewFFLayout("true")) d_ff_2 (
    .clk(MEM_WB_halt_2), .D(1'b1), .Q(halt), .en(1'b1), .reset(Go));  // open: Qn, preset
  Multiplexer #(.select(2), .width(32), .disabled("Z"), .enable("false")) multiplexer_7 (
    .in0(MEM_WB_aluresult_2), .in1(MEM_WB_readdata_2), .in2(MEM_WB_pc_4_2), .out(RDin), .sel(MEM_WB_memtoreg));  // open: in3

  // Other names for the same wires on the sheet: MEM_PC[31:0] = M_PC; WB_RegWrite = RegWrite

  // Notes on the sheet:
  //   中断源
  //   时空图监测，可删除
  //   中断等待指示
  //   数码管输出
  //   IF 阶段
  //   contents of 指令存储器 (hex, n*v repeats v):
  //   413 493 913 993 46413 14e493 296913 39e993 842023 942223 1242423 1342623 a00893 493 913 993 73
  //   BLTU
  //   JAL
  //   Jalr
  //   XOR
  //   LUI
  //   LH
  //   ecall
  //   rs1
  //   rs2
  //   imm12
  //   imm_sw
  //   imm_b
  //   imm_j
  //   rd
  //   Beq
  //   Bne
  //   MemToReg
  //   MemWrite
  //   AluOP
  //   AluSrcB
  //   RegWrite
  //   Stype
  //   ID 阶段
  //   JAL
  //   Jalr
  //   LUI
  //   LH
  //   BLTU
  //   控制位
  //   流水调试日志用
  //   暂停节拍，不能为0
  //   戳工具置1进入计数暂停模式，ctrl+k时钟自动运行到对应节拍暂停
  //   ctrl+k关闭时钟连续运行，将控制位置零，进入单步调试模式调试
  //   用这个时钟源需要去掉电路中的其他时钟源
  //   Beq
  //   Bne
  //   MemToReg
  //   MemWrite
  //   AluOP
  //   AluSrcB
  //   RegWrite
  //   Stype
  //   JAL
  //   Jalr
  //   BLTU
  //   可计数暂停的时钟源
  //   EX 阶段
  //   为方便自动评测，需要输出流水线各段保存的PC值，注意是PC不是PC+4，另外ID段寄存器写入信息，Mem段内存写入信息也要输出
  //   MemToReg
  //   MemWrite
  //   RegWrite
  //   halt
  //   ALUResult
  //   R2
  //   JAL
  //   Jalr
  //   MEM 阶段
  //   WB 阶段
  //   JAL
  //   Jalr
  //   MemToReg
  //   ALUResult
  //   MemDataOut
  //   WB.PC+4
endmodule

module \气泡流水线  (
  output RegWrite,
  output MemWrite,
  output [31:0] IF_PC,
  output [31:0] ID_PC,
  output [31:0] EX_PC,
  output [31:0] M_PC,
  output [31:0] WB_PC,
  output [31:0] RDin,
  output [31:0] MDin,
  output [31:0] LedData
);

  wire alu_1_equal, alu_1_out_6, and_1_out, and_2_out, and_3_out, and_4_out, and_5_out, and_7_out, CLK,
       clock_1_out, clock_2_out, comparator_1_eq, comparator_1_lt, comparator_2_eq, d_ff_1_q, ecall,
       EX_ecall, EX_halt, EX_MEM_halt_2, EX_MEM_jal_2, EX_MEM_jalr_2, EX_MEM_lh_2, EX_MEM_memtoreg_2,
       EX_MEM_regwrite_2, Go, halt, ID_EX_alusrcb_2, ID_EX_beq_2, ID_EX_bltu_2, ID_EX_bne_2, ID_EX_jal_2,
       ID_EX_lh_2, ID_EX_lui_2, ID_EX_memtoreg_2, ID_EX_memwrite_2, ID_EX_regwrite_2, IR1, IR2, IR3,
       MEM_WB_halt_2, MEM_WB_jal_2, MEM_WB_jalr_2, nand_1_out, not_1_out, not_2_out, not_3_out, not_4_out,
       not_5_out, not_6_out, not_7_out, not_8_out, or_1_out, or_3_out, RST, stall, W1, W2, W3,
       \单周期硬布线控制器_1_alu_src , \单周期硬布线控制器_1_beq , \单周期硬布线控制器_1_bltu , \单周期硬布线控制器_1_bne , \单周期硬布线控制器_1_jal ,
       \单周期硬布线控制器_1_jalr , \单周期硬布线控制器_1_lh , \单周期硬布线控制器_1_lui , \单周期硬布线控制器_1_memtoreg ,
       \单周期硬布线控制器_1_memwrite , \单周期硬布线控制器_1_regwrite , \单周期硬布线控制器_1_rs1_used , \单周期硬布线控制器_1_rs2_used ,
       \单周期硬布线控制器_1_s_type , \气泡处理逻辑_flush ;
  wire [1:0] ID_EX_jalr_2, MEM_WB_memtoreg;
  wire [3:0] ID_EX_aluop_2, \单周期硬布线控制器_1_alu_op ;
  wire [4:0] EX_MEM_rd_2, ID_EX_rd_2, multiplexer_2_out, multiplexer_3_out, WB_rd;
  wire [12:0] CNT_num;
  wire [15:0] \LoadUse次数 , multiplexer_8_out, \总周期数 , \插入气泡数 , \无条件分支数 , \条件分支成功数 ;
  wire [31:0] alu_1_result, ALU_addr, bit_extender_1_out, bit_extender_2_out, bit_extender_3_out,
       bit_extender_4_out, bit_extender_5_out, branch_addr, EX_IR, EX_MEM_pc_4_2, EX_MEM_result_2,
       ID_EX_imm_1_2, ID_EX_imm_2_2, ID_EX_pc_4_2, ID_EX_r1_2, ID_EX_r2_2, ID_IR, IF_ID_pc_4_2, IF_IR,
       MEM_IR, MEM_WB_aluresult_2, MEM_WB_pc_4_2, MEM_WB_readdata_2, multiplexer_1_out, multiplexer_4_out,
       multiplexer_5_out, multiplexer_6_out, multiplexer_9_out, PC_4, ram_1_data, regifile_1_r1,
       regifile_1_r2, shifter_1_out, WB_IR;

  Button \u_总复位  (.out(RST));
  Button _1 (.out(IR1));
  Button _2 (.out(IR2));
  Button _3 (.out(IR3));
  // Probe on \总周期数 
  // Probe on \总周期数 
  Button \u_继续运行  (.out(Go));
  LED #(.active("true")) led_1 (.in(W1));
  LED #(.active("true")) led_2 (.in(W2));
  LED #(.active("true")) led_3 (.in(W3));
  \气泡处理逻辑  \u_气泡处理逻辑  (
    .BranchTaken(or_3_out), .IR(ID_IR), .ecall(ecall), .rs1_used(\单周期硬布线控制器_1_rs1_used ),
    .EX_RegWrite(ID_EX_regwrite_2), .EX_rd(ID_EX_rd_2), .rs2_used(\单周期硬布线控制器_1_rs2_used ),
    .MEM_RegWrite(EX_MEM_regwrite_2), .MEM_rd(EX_MEM_rd_2), .stall(stall), .flush(\气泡处理逻辑_flush ));
  not not_1 (not_1_out, stall);
  not not_2 (not_2_out, halt);
  and and_1 (and_1_out, not_2_out, not_1_out);
  Hex_Digit_Display hex_digit_display_1 (.value(LedData[31:28]));  // open: dp
  // Probe on IF_PC[19:0]
  // RiscV_Probe riscv_probe_1: pin names not known; wires that end beside it: IF_IR
  Multiplexer #(.select(2), .width(32), .disabled("Z"), .enable("false")) multiplexer_1 (
    .in0(PC_4), .in1(ALU_addr), .in2(branch_addr), .out(multiplexer_1_out), .sel(ID_EX_jalr_2));  // open: in3
  Register #(.width(32), .trigger("rising"), .Select("low")) PC (
    .D(multiplexer_1_out), .en(and_1_out), .Q(IF_PC), .clk(CLK), .clr(RST));
  Hex_Digit_Display hex_digit_display_2 (.value(LedData[27:24]));  // open: dp
  Hex_Digit_Display hex_digit_display_3 (.value(LedData[23:20]));  // open: dp
  // Probe on ID_PC[19:0]
  // RiscV_Probe riscv_probe_2: pin names not known; wires that end beside it: ID_IR
  // RiscV_Probe riscv_probe_3: pin names not known; wires that end beside it: IF_IR, stall, halt, RST
  Adder #(.width(32)) adder_1 (.a(IF_PC), .b(32'h4), .out(PC_4));  // open: cin, cout
  Hex_Digit_Display hex_digit_display_4 (.value(LedData[19:16]));  // open: dp
  Hex_Digit_Display hex_digit_display_5 (.value(LedData[15:12]));  // open: dp
  ROM #(.addrWidth(10), .dataWidth(32), .Select("high")) \u_指令存储器  (.addr(IF_PC[11:2]), .data(IF_IR));
  and and_2 (and_2_out, ~stall, ~halt);  // AND_Gate
  Hex_Digit_Display hex_digit_display_6 (.value(LedData[11:8]));  // open: dp
  Hex_Digit_Display hex_digit_display_7 (.value(LedData[7:4]));  // open: dp
  Clock #(.highDuration(1), .lowDuration(1)) clock_1 (.out(clock_1_out));
  // Probe on EX_PC[19:0]
  // RiscV_Probe riscv_probe_4: pin names not known; wires that end beside it: clock_1_out, EX_IR, CLK
  or or_1 (or_1_out, ID_EX_jalr_2[1], ID_EX_jalr_2[0]);
  IF_ID IF_ID (
    .IR(IF_IR), .PC(IF_PC), .PC_4(PC_4), .IR_2(ID_IR), .PC_2(ID_PC), .PC_4_2(IF_ID_pc_4_2), .reset(RST),
    .en(and_2_out), .clk(CLK), .BranchTaken(or_1_out));
  Hex_Digit_Display hex_digit_display_8 (.value(LedData[3:0]));  // open: dp
  // Probe on \总周期数 
  // Probe on M_PC[19:0]
  // RiscV_Probe riscv_probe_5: pin names not known; wires that end beside it: MEM_IR
  \单周期硬布线控制器  \u_单周期硬布线控制器_1  (
    .Funct({ID_IR[30], ID_IR[25], ID_IR[14:12]}), .OP(ID_IR[6:2]), .ALU_OP(\单周期硬布线控制器_1_alu_op ),
    .MemToReg(\单周期硬布线控制器_1_memtoreg ), .MemWrite(\单周期硬布线控制器_1_memwrite ), .ALU_SRC(\单周期硬布线控制器_1_alu_src ),
    .RegWrite(\单周期硬布线控制器_1_regwrite ), .ecall(ecall), .S_type(\单周期硬布线控制器_1_s_type ),
    .Jalr(\单周期硬布线控制器_1_jalr ), .Beq(\单周期硬布线控制器_1_beq ), .JAL(\单周期硬布线控制器_1_jal ), .Bne(\单周期硬布线控制器_1_bne ),
    .BLTU(\单周期硬布线控制器_1_bltu ), .LUI(\单周期硬布线控制器_1_lui ), .LH(\单周期硬布线控制器_1_lh ),
    .RS1_USED(\单周期硬布线控制器_1_rs1_used ), .RS2_USED(\单周期硬布线控制器_1_rs2_used ), .in_3(ID_IR[21]));  // open: XOR, uret
  assign bit_extender_1_out = {{20{ID_IR[31]}}, ID_IR[31:20]};  // Bit_Extender bit_extender_1
  assign bit_extender_2_out = {{20{ID_IR[31]}}, {ID_IR[31:25], ID_IR[11:7]}};  // Bit_Extender bit_extender_2
  assign bit_extender_3_out = {{20{ID_IR[31]}}, {ID_IR[31], ID_IR[7], ID_IR[30:25], ID_IR[11:8]}};  // Bit_Extender bit_extender_3
  assign bit_extender_4_out = {{12{ID_IR[31]}}, {ID_IR[31], ID_IR[19:12], ID_IR[20], ID_IR[30:21]}};  // Bit_Extender bit_extender_4
  // Probe on \总周期数 
  // Probe on \无条件分支数 
  // Probe on \条件分支成功数 
  // Probe on \插入气泡数 
  // Probe on \LoadUse次数 
  Multiplexer #(.select(1), .width(5), .disabled("Z"), .enable("false")) multiplexer_2 (
    .in0(ID_IR[19:15]), .in1(5'b10001), .out(multiplexer_2_out), .sel(ecall));
  Multiplexer #(.select(1), .width(5), .disabled("Z"), .enable("false")) multiplexer_3 (
    .in0(ID_IR[24:20]), .in1(5'b01010), .out(multiplexer_3_out), .sel(ecall));
  Multiplexer #(.select(1), .width(32), .disabled("Z"), .enable("false")) multiplexer_4 (
    .in0(bit_extender_1_out), .in1(bit_extender_2_out), .out(multiplexer_4_out), .sel(\单周期硬布线控制器_1_s_type ));
  // Probe on IF_PC[11:0]
  // Probe on WB_PC[19:0]
  // RiscV_Probe riscv_probe_6: pin names not known; wires that end beside it: WB_IR
  Multiplexer #(.select(1), .width(32), .disabled("Z"), .enable("false")) multiplexer_5 (
    .in0(bit_extender_3_out), .in1(bit_extender_4_out), .out(multiplexer_5_out), .sel(\单周期硬布线控制器_1_jal ));
  // Probe on ID_PC[11:0]
  // Probe on EX_PC[11:0]
  not not_3 (not_3_out, CLK);
  // Probe on M_PC[11:0]
  D_Flip_Flop #(.trigger("high"), .Pre_Clr_Positions("LEGACY"), .NegatePresetClear("false"), .enable("true"), .NewFFLayout("false")) d_ff_1 (.Q(d_ff_1_q));  // open: clk, D, Qn, preset, en, reset
  // Probe on 13'hc
  ID_EX ID_EX (
    .Beq(\单周期硬布线控制器_1_beq ), .Bne(\单周期硬布线控制器_1_bne ), .MemToReg(\单周期硬布线控制器_1_memtoreg ),
    .MemWrite(\单周期硬布线控制器_1_memwrite ), .AluSrcB(\单周期硬布线控制器_1_alu_src ), .RegWrite(\单周期硬布线控制器_1_regwrite ),
    .SType(\单周期硬布线控制器_1_s_type ), .ecall(ecall), .Jal(\单周期硬布线控制器_1_jal ), .Jalr(\单周期硬布线控制器_1_jalr ),
    .LUI(\单周期硬布线控制器_1_lui ), .LH(\单周期硬布线控制器_1_lh ), .BLTU(\单周期硬布线控制器_1_bltu ), .AluOP(\单周期硬布线控制器_1_alu_op ),
    .rd(ID_IR[11:7]), .R1(regifile_1_r1), .R2(regifile_1_r2), .imm_1(multiplexer_4_out),
    .imm_2(multiplexer_5_out), .PC(ID_PC), .PC_4(IF_ID_pc_4_2), .IR(ID_IR), .Beq_2(ID_EX_beq_2),
    .Bne_2(ID_EX_bne_2), .MemToReg_2(ID_EX_memtoreg_2), .MemWrite_2(ID_EX_memwrite_2),
    .AluSrcB_2(ID_EX_alusrcb_2), .RegWrite_2(ID_EX_regwrite_2), .ecall_2(EX_ecall), .Jal_2(ID_EX_jal_2),
    .Jalr_2(ID_EX_jalr_2[0]), .LUI_2(ID_EX_lui_2), .LH_2(ID_EX_lh_2), .BLTU_2(ID_EX_bltu_2),
    .AluOP_2(ID_EX_aluop_2), .rd_2(ID_EX_rd_2), .R1_2(ID_EX_r1_2), .R2_2(ID_EX_r2_2),
    .imm_1_2(ID_EX_imm_1_2), .imm_2_2(ID_EX_imm_2_2), .PC_2(EX_PC), .PC_4_2(ID_EX_pc_4_2), .IR_2(EX_IR),
    .reset(RST), .en(not_4_out), .clk(CLK), .flush(\气泡处理逻辑_flush ));  // open: RS1_Forward, RS2_Forward, SType_2, RS1_Forward_2, RS2_Forward_2
  Regifile regifile_1 (
    .Din(RDin), .Clk(not_3_out), .R1(regifile_1_r1), .R2(regifile_1_r2), .WE(RegWrite), .W_num(WB_rd),
    .R1_num(multiplexer_2_out), .R2_num(multiplexer_3_out));
  not not_4 (not_4_out, halt);
  // Probe on WB_PC[11:0]
  Comparator #(.width(13), .mode("twosComplement")) comparator_1 (
    .a(CNT_num), .b(13'hc), .eq(comparator_1_eq), .lt(comparator_1_lt));  // open: gt
  Clock #(.highDuration(1), .lowDuration(1)) clock_2 (.out(clock_2_out));
  nand nand_1 (nand_1_out, d_ff_1_q, comparator_1_eq);
  Counter #(.width(13), .max('h1fff), .ongoal("stay"), .trigger("rising"), .behavior("old")) counter_1 (
    .count(comparator_1_lt), .Q(CNT_num), .clk(clock_2_out));  // open: load, D, carry, clr, preset
  Shifter #(.width(32), .shift("ll")) shifter_1 (.in(ID_EX_imm_2_2), .\dist (5'b00001), .out(shifter_1_out));
  Comparator #(.width(32), .mode("twosComplement")) comparator_2 (
    .a(ID_EX_r1_2), .b(32'ha), .eq(comparator_2_eq));  // open: gt, lt
  assign CLK = nand_1_out ? clock_2_out : 1'bz;  // Controlled_Buffer controlled_buffer_1
  or or_2 (ID_EX_jalr_2[1], and_4_out, ID_EX_jal_2, and_3_out, and_5_out);
  and and_3 (and_3_out, ID_EX_bne_2, ~alu_1_equal);  // AND_Gate
  and and_4 (and_4_out, ID_EX_beq_2, alu_1_equal);
  Multiplexer #(.select(1), .width(32), .disabled("Z"), .enable("false")) multiplexer_6 (
    .in0(ID_EX_r2_2), .in1(ID_EX_imm_1_2), .out(multiplexer_6_out), .sel(ID_EX_alusrcb_2));
  not not_5 (not_5_out, comparator_2_eq);
  Pull_Resistor #(.pull(1)) pull_resistor_1 (.node(CLK));
  or or_3 (or_3_out, ID_EX_jalr_2[1], ID_EX_jalr_2[0]);
  and and_5 (and_5_out, alu_1_out_6, ID_EX_bltu_2);
  ALU alu_1 (
    .X(ID_EX_r1_2), .Y(multiplexer_6_out), .AluOP(ID_EX_aluop_2), .Equal(alu_1_equal), .Result(alu_1_result),
    .out_6(alu_1_out_6));  // open: Result_2, out_4
  Adder #(.width(32)) adder_2 (.a(shifter_1_out), .b(EX_PC), .out(branch_addr));  // open: cin, cout
  and and_6 (EX_halt, comparator_2_eq, EX_ecall);
  Register #(.width(32), .trigger("rising"), .Select("low")) PC_2 (
    .D(ID_EX_r2_2), .en(and_7_out), .Q(LedData), .clk(CLK));  // open: clr
  and and_7 (and_7_out, not_5_out, EX_ecall);
  not not_6 (not_6_out, halt);
  Multiplexer #(.select(1), .width(32), .disabled("Z"), .enable("false")) multiplexer_7 (
    .in0(alu_1_result), .in1({EX_IR[31:12], {12{1'b0}}}), .out(ALU_addr), .sel(ID_EX_lui_2));
  not not_7 (not_7_out, halt);
  Counter #(.width(16), .max('hffff), .ongoal("wrap"), .trigger("rising"), .behavior("new")) counter_2 (
    .count(not_6_out), .Q(\总周期数 ), .clk(CLK));  // open: load, D, carry, clr, preset, down
  EX_MEM EX_MEM (
    .JAL(ID_EX_jal_2), .Jalr(ID_EX_jalr_2[0]), .MemToReg(ID_EX_memtoreg_2), .MemWrite(ID_EX_memwrite_2),
    .RegWrite(ID_EX_regwrite_2), .halt(EX_halt), .rd(ID_EX_rd_2), .result(ALU_addr), .WriteData(ID_EX_r2_2),
    .IR(EX_IR), .PC(EX_PC), .PC_4(ID_EX_pc_4_2), .JAL_2(EX_MEM_jal_2), .Jalr_2(EX_MEM_jalr_2),
    .MemToReg_2(EX_MEM_memtoreg_2), .MemWrite_2(MemWrite), .RegWrite_2(EX_MEM_regwrite_2),
    .halt_2(EX_MEM_halt_2), .rd_2(EX_MEM_rd_2), .result_2(EX_MEM_result_2), .WriteData_2(MDin),
    .IR_2(MEM_IR), .PC_2(M_PC), .PC_4_2(EX_MEM_pc_4_2), .reset(RST), .en(not_7_out), .clk(CLK),
    .LH(ID_EX_lh_2), .LH_2(EX_MEM_lh_2));
  RAM #(.addrWidth(10), .dataWidth(32), .bus("separate"), .Select("high")) ram_1 (
    .addr(EX_MEM_result_2[11:2]), .din(MDin), .data(ram_1_data), .str(MemWrite), .sel(1'b1), .clk(CLK),
    .ld(1'b1), .clr(RST));
  Multiplexer #(.select(1), .width(16), .disabled("Z"), .enable("false")) multiplexer_8 (
    .in0(ram_1_data[15:0]), .in1(ram_1_data[31:16]), .out(multiplexer_8_out), .sel(EX_MEM_result_2[1]));
  Multiplexer #(.select(1), .width(32), .disabled("Z"), .enable("false")) multiplexer_9 (
    .in0(ram_1_data), .in1(bit_extender_5_out), .out(multiplexer_9_out), .sel(EX_MEM_lh_2));
  assign bit_extender_5_out = {{16{multiplexer_8_out[15]}}, multiplexer_8_out};  // Bit_Extender bit_extender_5
  not not_8 (not_8_out, halt);
  MEM_WB MEM_WB (
    .Jal(EX_MEM_jal_2), .Jalr(EX_MEM_jalr_2), .MenToReg(EX_MEM_memtoreg_2), .RegWrite(EX_MEM_regwrite_2),
    .halt(EX_MEM_halt_2), .rd(EX_MEM_rd_2), .ALUResult(EX_MEM_result_2), .ReadData(multiplexer_9_out),
    .IR(MEM_IR), .PC(M_PC), .PC_4(EX_MEM_pc_4_2), .Jal_2(MEM_WB_jal_2), .Jalr_2(MEM_WB_jalr_2),
    .MemToReg(MEM_WB_memtoreg[0]), .RegWrite_2(RegWrite), .halt_2(MEM_WB_halt_2), .rd_2(WB_rd),
    .ALUResult_2(MEM_WB_aluresult_2), .ReadData_2(MEM_WB_readdata_2), .IR_2(WB_IR), .PC_2(WB_PC),
    .PC_4_2(MEM_WB_pc_4_2), .reset(RST), .en(not_8_out), .clk(CLK));
  or or_4 (MEM_WB_memtoreg[1], MEM_WB_jal_2, MEM_WB_jalr_2);
  D_Flip_Flop #(.trigger("rising"), .Pre_Clr_Positions("ABOVE_BELOW"), .NegatePresetClear("false"), .enable("true"), .NewFFLayout("true")) d_ff_2 (
    .clk(MEM_WB_halt_2), .D(1'b1), .Q(halt), .en(1'b1), .reset(Go));  // open: Qn, preset
  Multiplexer #(.select(2), .width(32), .disabled("Z"), .enable("false")) multiplexer_10 (
    .in0(MEM_WB_aluresult_2), .in1(MEM_WB_readdata_2), .in2(MEM_WB_pc_4_2), .out(RDin), .sel(MEM_WB_memtoreg));  // open: in3

  // Other names for the same wires on the sheet: MEM_PC[31:0] = M_PC; WB_RegWrite = RegWrite

  // Notes on the sheet:
  //   中断源
  //   时空图监测，可删除
  //   中断等待指示
  //   数码管输出
  //   IF 阶段
  //   contents of 指令存储器 (hex, n*v repeats v):
  //   100493 100006f 100493 200913 300993 100006f 100493 200913 300993 100006f 100493 200913 300993
  //   100006f 100493 200913 300993 3e4000ef 100413 100493 1f49493 900533 2200893 73 24d493 48463 fedff06f
  //   900533 2200893 73 100493 249493 900533 2200893 73 48463 fedff06f 100493 1f49493 900533 2200893 73
  //   4034d493 900533 2200893 73 4044d493 900533 2200893 73 4044d493 900533 2200893 73 4044d493 900533
  //   2200893 73 4044d493 900533 2200893 73 4044d493 900533 2200893 73 4044d493 900533 2200893 73 4044d493
  //   900533 2200893 73 100413 1f41993 41f9d993 433 c00913 300b13 140413 f47413 800293 100313 499993
  //   89e9b3 1300533 2200893 73 406282b3 fe0294e3 140413 f00f93 1f47433 1c41413 800293 100313 49d993
  //   89e9b3 1300533 2200893 73 406282b3 fe0294e3 1c45413 406b0b33 b0463 f95ff06f 2b3 fff2c293 829293
  //   ff2e293 500533 2200893 73 fff00413 493 84a023 140413 448493 84a023 140413 448493 84a023 140413
  //   448493 84a023 140413 448493 84a023 140413 448493 84a023 140413 448493 84a023 140413 448493 84a023
  //   140413 448493 84a023 140413 448493 84a023 140413 448493 84a023 140413 448493 84a023 140413 448493
  //   84a023 140413 448493 84a023 140413 448493 84a023 140413 448493 84a023 140413 448493 140413 433
  //   3c00493 42983 4aa03 149a2b3 28663 134a023 1442023 ffc48493 fe9412e3 800533 2200893 73 440413 3c00493
  //   fc9416e3 a00893 73 fff00293 7700493 849493 7748493 900533 2200893 73 1000e13 54c4b3 900533 2200893
  //   73 fffe0e13 fe0e16e3 a00893 73 800e13 fedc04b7 fff00413 1045413 84e4b3 900533 2200893 73 ba9804b7
  //   900533 73 765404b7 900533 73 321004b7 900533 73 fffe0e13 fa0e1ee3 a00893 73 313 1000e13 8400493
  //   849493 8348493 400913 891913 490913 849493 8248493 849493 8148493 891913 490913 891913 490913 932023
  //   12484b3 430313 fffe0e13 fe0e18e3 2000e13 313 31483 900533 2200893 73 230313 fffe0e13 fe0e14e3 a00893
  //   73 ff100493 900533 2200893 73 148493 fe9068e3 900533 2200893 73 a00893 73 a00893 73 413 140413
  //   800533 2200893 73 240413 800533 2200893 73 340413 800533 2200893 73 440413 800533 2200893 73 540413
  //   800533 2200893 73 640413 800533 2200893 73 740413 800533 2200893 73 840413 800533 2200893 2200893 73
  //   8067
  //   rs1-used
  //   JAL
  //   Jalr
  //   XOR
  //   LUI
  //   LH
  //   BLTU
  //   rs1
  //   rs2
  //   imm12
  //   imm_sw
  //   rd
  //   ecall
  //   rs2-used
  //   Beq
  //   Bne
  //   MemToReg
  //   MemWrite
  //   AluOP
  //   AluSrcB
  //   RegWrite
  //   Stype
  //   ecall
  //   imm_b
  //   imm_j
  //   ID 阶段
  //   JAL
  //   Jalr
  //   LUI
  //   LH
  //   BLTU
  //   控制位
  //   流水调试日志用
  //   暂停节拍，不能为0
  //   Beq
  //   Bne
  //   AluOP
  //   Stype
  //   戳工具置1进入计数暂停模式，ctrl+k时钟自动运行到对应节拍暂停
  //   ctrl+k关闭时钟连续运行，将控制位置零，进入单步调试模式调试
  //   EX 阶段
  //   JAL
  //   Jalr
  //   MemToReg
  //   MemWrite
  //   LUI
  //   LH
  //   AluSrcB
  //   BLTU
  //   RegWrite
  //   可计数暂停的时钟源
  //   LUI 指令支持电路
  //   MemToReg
  //   MemWrite
  //   LH
  //   RegWrite
  //   halt
  //   ALUResult
  //   R2
  //   为方便自动评测，需要输出流水线各段保存的PC值，注意是PC不是PC+4，另外ID段寄存器写入信息，Mem段内存写入信息也要输出
  //   JAL
  //   Jalr
  //   MEM 阶段
  //   LH 指令支持电路
  //   JAL
  //   Jalr
  //   MemToReg
  //   ALUResult
  //   MemDataOut
  //   WB.PC+4
  //   WB 阶段
endmodule
module \重定向流水线  (
  output RegWrite,
  output MemWrite,
  output [31:0] IF_PC,
  output [31:0] ID_PC,
  output [31:0] EX_PC,
  output [31:0] M_PC,
  output [31:0] WB_PC,
  output [31:0] RDin,
  output [31:0] MDin,
  output [31:0] LedData
);

  wire alu_1_equal, alu_1_out_6, and_1_out, and_2_out, and_3_out, and_4_out, and_6_out, and_7_out, CLK,
       clock_1_out, clock_2_out, comparator_1_eq, comparator_1_lt, comparator_2_eq, d_ff_1_q, ecall,
       EX_ecall, EX_halt, EX_MEM_halt_2, EX_MEM_jal_2, EX_MEM_jalr_2, EX_MEM_lh_2, EX_MEM_memtoreg_2,
       EX_MEM_regwrite_2, Go, halt, ID_EX_alusrcb_2, ID_EX_beq_2, ID_EX_bltu_2, ID_EX_bne_2, ID_EX_jal_2,
       ID_EX_lh_2, ID_EX_lui_2, ID_EX_memtoreg_2, ID_EX_memwrite_2, ID_EX_regwrite_2, IR1, IR2, IR3,
       MEM_WB_halt_2, MEM_WB_jal_2, MEM_WB_jalr_2, nand_1_out, not_1_out, not_2_out, not_3_out, not_4_out,
       not_5_out, not_6_out, not_7_out, not_8_out, or_1_out, or_3_out, RST, stall, W1, W2, W3,
       \单周期硬布线控制器_1_alu_src , \单周期硬布线控制器_1_beq , \单周期硬布线控制器_1_bltu , \单周期硬布线控制器_1_bne , \单周期硬布线控制器_1_jal ,
       \单周期硬布线控制器_1_jalr , \单周期硬布线控制器_1_lh , \单周期硬布线控制器_1_lui , \单周期硬布线控制器_1_memtoreg ,
       \单周期硬布线控制器_1_memwrite , \单周期硬布线控制器_1_regwrite , \单周期硬布线控制器_1_rs1_used , \单周期硬布线控制器_1_rs2_used ,
       \单周期硬布线控制器_1_s_type , \重定向处理逻辑_flush ;
  wire [1:0] ID_EX_jalr_2, ID_EX_rs1_forward_2, ID_EX_rs2_forward_2, MEM_WB_memtoreg, \重定向处理逻辑_rs1forward ,
       \重定向处理逻辑_rs2forward ;
  wire [3:0] ID_EX_aluop_2, \单周期硬布线控制器_1_alu_op ;
  wire [4:0] EX_MEM_rd_2, ID_EX_rd_2, multiplexer_2_out, multiplexer_3_out, WB_rd;
  wire [12:0] CNT_num;
  wire [15:0] \LoadUse次数 , multiplexer_10_out, \总周期数 , \插入气泡数 , \无条件分支数 , \条件分支成功数 ;
  wire [31:0] alu_1_result, ALU_addr, bit_extender_1_out, bit_extender_2_out, bit_extender_3_out,
       bit_extender_4_out, bit_extender_5_out, branch_addr, EX_IR, EX_MEM_pc_4_2, ID_EX_imm_1_2,
       ID_EX_imm_2_2, ID_EX_pc_4_2, ID_EX_r1_2, ID_EX_r2_2, ID_IR, IF_ID_pc_4_2, IF_IR, MEM_aluResult,
       MEM_IR, MEM_WB_aluresult_2, MEM_WB_pc_4_2, MEM_WB_readdata_2, multiplexer_1_out, multiplexer_4_out,
       multiplexer_5_out, multiplexer_6_out, multiplexer_7_out, multiplexer_8_out, multiplexer_11_out, PC_4,
       ram_1_data, regifile_1_r1, regifile_1_r2, shifter_1_out, WB_IR;

  Button \u_总复位  (.out(RST));
  Button _1 (.out(IR1));
  Button _2 (.out(IR2));
  Button _3 (.out(IR3));
  // Probe on \总周期数 
  // Probe on \总周期数 
  Button \u_继续运行  (.out(Go));
  LED #(.active("true")) led_1 (.in(W1));
  LED #(.active("true")) led_2 (.in(W2));
  LED #(.active("true")) led_3 (.in(W3));
  \重定向处理逻辑  \u_重定向处理逻辑  (
    .BranchTaken(or_3_out), .IR(ID_IR), .EX_MemToReg(ID_EX_memtoreg_2), .rs1_used(\单周期硬布线控制器_1_rs1_used ),
    .EX_RegWrite(ID_EX_regwrite_2), .EX_rd(ID_EX_rd_2), .rs2_used(\单周期硬布线控制器_1_rs2_used ),
    .MEM_RegWrite(EX_MEM_regwrite_2), .MEM_rd(EX_MEM_rd_2), .stall(stall), .rs1Forward(\重定向处理逻辑_rs1forward ),
    .flush(\重定向处理逻辑_flush ), .rs2Forward(\重定向处理逻辑_rs2forward ), .ecall(ecall));
  not not_1 (not_1_out, halt);
  not not_2 (not_2_out, stall);
  and and_1 (and_1_out, not_1_out, not_2_out);
  Hex_Digit_Display hex_digit_display_1 (.value(LedData[31:28]));  // open: dp
  // Probe on IF_PC[19:0]
  // RiscV_Probe riscv_probe_1: pin names not known; wires that end beside it: IF_IR
  Multiplexer #(.select(2), .width(32), .disabled("Z"), .enable("false")) multiplexer_1 (
    .in0(PC_4), .in1(ALU_addr), .in2(branch_addr), .out(multiplexer_1_out), .sel(ID_EX_jalr_2));  // open: in3
  Register #(.width(32), .trigger("rising"), .Select("low")) PC (
    .D(multiplexer_1_out), .en(and_1_out), .Q(IF_PC), .clk(CLK), .clr(RST));
  Hex_Digit_Display hex_digit_display_2 (.value(LedData[23:20]));  // open: dp
  Hex_Digit_Display hex_digit_display_3 (.value(LedData[27:24]));  // open: dp
  // Probe on ID_PC[19:0]
  // RiscV_Probe riscv_probe_2: pin names not known; wires that end beside it: ID_IR
  // RiscV_Probe riscv_probe_3: pin names not known; wires that end beside it: IF_IR, RST
  Adder #(.width(32)) adder_1 (.a(IF_PC), .b(32'h4), .out(PC_4));  // open: cin, cout
  Hex_Digit_Display hex_digit_display_4 (.value(LedData[15:12]));  // open: dp
  Hex_Digit_Display hex_digit_display_5 (.value(LedData[19:16]));  // open: dp
  ROM #(.addrWidth(10), .dataWidth(32), .Select("high")) \u_指令存储器  (.addr(IF_PC[11:2]), .data(IF_IR));
  and and_2 (and_2_out, ~stall, ~halt);  // AND_Gate
  Hex_Digit_Display hex_digit_display_6 (.value(LedData[11:8]));  // open: dp
  Hex_Digit_Display hex_digit_display_7 (.value(LedData[7:4]));  // open: dp
  Clock #(.highDuration(1), .lowDuration(1)) clock_1 (.out(clock_1_out));
  // Probe on EX_PC[19:0]
  // RiscV_Probe riscv_probe_4: pin names not known; wires that end beside it: clock_1_out, EX_IR, CLK
  or or_1 (or_1_out, ID_EX_jalr_2[1], ID_EX_jalr_2[0]);
  IF_ID IF_ID (
    .IR(IF_IR), .PC(IF_PC), .PC_4(PC_4), .IR_2(ID_IR), .PC_2(ID_PC), .PC_4_2(IF_ID_pc_4_2), .reset(RST),
    .en(and_2_out), .clk(CLK), .BranchTaken(or_1_out));
  Hex_Digit_Display hex_digit_display_8 (.value(LedData[3:0]));  // open: dp
  // Probe on \总周期数 
  // Probe on M_PC[19:0]
  // RiscV_Probe riscv_probe_5: pin names not known; wires that end beside it: MEM_IR
  \单周期硬布线控制器  \u_单周期硬布线控制器_1  (
    .Funct({ID_IR[30], ID_IR[25], ID_IR[14:12]}), .OP(ID_IR[6:2]), .ALU_OP(\单周期硬布线控制器_1_alu_op ),
    .MemToReg(\单周期硬布线控制器_1_memtoreg ), .MemWrite(\单周期硬布线控制器_1_memwrite ), .ALU_SRC(\单周期硬布线控制器_1_alu_src ),
    .RegWrite(\单周期硬布线控制器_1_regwrite ), .ecall(ecall), .S_type(\单周期硬布线控制器_1_s_type ),
    .Jalr(\单周期硬布线控制器_1_jalr ), .Beq(\单周期硬布线控制器_1_beq ), .JAL(\单周期硬布线控制器_1_jal ), .Bne(\单周期硬布线控制器_1_bne ),
    .BLTU(\单周期硬布线控制器_1_bltu ), .LUI(\单周期硬布线控制器_1_lui ), .LH(\单周期硬布线控制器_1_lh ),
    .RS1_USED(\单周期硬布线控制器_1_rs1_used ), .RS2_USED(\单周期硬布线控制器_1_rs2_used ), .in_3(ID_IR[21]));  // open: XOR, uret
  assign bit_extender_1_out = {{20{ID_IR[31]}}, ID_IR[31:20]};  // Bit_Extender bit_extender_1
  assign bit_extender_2_out = {{20{ID_IR[31]}}, {ID_IR[31:25], ID_IR[11:7]}};  // Bit_Extender bit_extender_2
  assign bit_extender_3_out = {{20{ID_IR[31]}}, {ID_IR[31], ID_IR[7], ID_IR[30:25], ID_IR[11:8]}};  // Bit_Extender bit_extender_3
  assign bit_extender_4_out = {{12{ID_IR[31]}}, {ID_IR[31], ID_IR[19:12], ID_IR[20], ID_IR[30:21]}};  // Bit_Extender bit_extender_4
  // Probe on \总周期数 
  // Probe on \无条件分支数 
  // Probe on \条件分支成功数 
  // Probe on \插入气泡数 
  // Probe on \LoadUse次数 
  Multiplexer #(.select(1), .width(5), .disabled("Z"), .enable("false")) multiplexer_2 (
    .in0(ID_IR[19:15]), .in1(5'b10001), .out(multiplexer_2_out), .sel(ecall));
  Multiplexer #(.select(1), .width(5), .disabled("Z"), .enable("false")) multiplexer_3 (
    .in0(ID_IR[24:20]), .in1(5'b01010), .out(multiplexer_3_out), .sel(ecall));
  Multiplexer #(.select(1), .width(32), .disabled("Z"), .enable("false")) multiplexer_4 (
    .in0(bit_extender_1_out), .in1(bit_extender_2_out), .out(multiplexer_4_out), .sel(\单周期硬布线控制器_1_s_type ));
  // Probe on IF_PC[11:0]
  // Probe on WB_PC[19:0]
  // RiscV_Probe riscv_probe_6: pin names not known; wires that end beside it: WB_IR
  Multiplexer #(.select(1), .width(32), .disabled("Z"), .enable("false")) multiplexer_5 (
    .in0(bit_extender_3_out), .in1(bit_extender_4_out), .out(multiplexer_5_out), .sel(\单周期硬布线控制器_1_jal ));
  // Probe on EX_PC[11:0]
  // Probe on ID_PC[11:0]
  not not_3 (not_3_out, CLK);
  // Probe on M_PC[11:0]
  D_Flip_Flop #(.trigger("high"), .Pre_Clr_Positions("LEGACY"), .NegatePresetClear("false"), .enable("true"), .NewFFLayout("false")) d_ff_1 (.Q(d_ff_1_q));  // open: clk, D, Qn, preset, en, reset
  // Probe on 13'h8f5
  ID_EX ID_EX (
    .Beq(\单周期硬布线控制器_1_beq ), .Bne(\单周期硬布线控制器_1_bne ), .MemToReg(\单周期硬布线控制器_1_memtoreg ),
    .MemWrite(\单周期硬布线控制器_1_memwrite ), .AluSrcB(\单周期硬布线控制器_1_alu_src ), .RegWrite(\单周期硬布线控制器_1_regwrite ),
    .SType(\单周期硬布线控制器_1_s_type ), .ecall(ecall), .Jal(\单周期硬布线控制器_1_jal ), .Jalr(\单周期硬布线控制器_1_jalr ),
    .LUI(\单周期硬布线控制器_1_lui ), .LH(\单周期硬布线控制器_1_lh ), .BLTU(\单周期硬布线控制器_1_bltu ), .AluOP(\单周期硬布线控制器_1_alu_op ),
    .rd(ID_IR[11:7]), .R1(regifile_1_r1), .R2(regifile_1_r2), .imm_1(multiplexer_4_out),
    .imm_2(multiplexer_5_out), .PC(ID_PC), .PC_4(IF_ID_pc_4_2), .IR(ID_IR),
    .RS1_Forward(\重定向处理逻辑_rs1forward ), .RS2_Forward(\重定向处理逻辑_rs2forward ), .Beq_2(ID_EX_beq_2),
    .Bne_2(ID_EX_bne_2), .MemToReg_2(ID_EX_memtoreg_2), .MemWrite_2(ID_EX_memwrite_2),
    .AluSrcB_2(ID_EX_alusrcb_2), .RegWrite_2(ID_EX_regwrite_2), .ecall_2(EX_ecall), .Jal_2(ID_EX_jal_2),
    .Jalr_2(ID_EX_jalr_2[0]), .LUI_2(ID_EX_lui_2), .LH_2(ID_EX_lh_2), .BLTU_2(ID_EX_bltu_2),
    .AluOP_2(ID_EX_aluop_2), .rd_2(ID_EX_rd_2), .R1_2(ID_EX_r1_2), .R2_2(ID_EX_r2_2),
    .imm_1_2(ID_EX_imm_1_2), .imm_2_2(ID_EX_imm_2_2), .PC_2(EX_PC), .PC_4_2(ID_EX_pc_4_2), .IR_2(EX_IR),
    .RS1_Forward_2(ID_EX_rs1_forward_2), .RS2_Forward_2(ID_EX_rs2_forward_2), .reset(RST), .en(not_4_out),
    .clk(CLK), .flush(\重定向处理逻辑_flush ));  // open: SType_2
  Regifile regifile_1 (
    .Din(RDin), .Clk(not_3_out), .R1(regifile_1_r1), .R2(regifile_1_r2), .WE(RegWrite), .W_num(WB_rd),
    .R1_num(multiplexer_2_out), .R2_num(multiplexer_3_out));
  not not_4 (not_4_out, halt);
  // Probe on WB_PC[11:0]
  Comparator #(.width(13), .mode("twosComplement")) comparator_1 (
    .a(CNT_num), .b(13'h8f5), .eq(comparator_1_eq), .lt(comparator_1_lt));  // open: gt
  Clock #(.highDuration(1), .lowDuration(1)) clock_2 (.out(clock_2_out));
  nand nand_1 (nand_1_out, d_ff_1_q, comparator_1_eq);
  Counter #(.width(13), .max('h1fff), .ongoal("stay"), .trigger("rising"), .behavior("old")) counter_1 (
    .count(comparator_1_lt), .Q(CNT_num), .clk(clock_2_out));  // open: load, D, carry, clr, preset
  Multiplexer #(.select(2), .width(32), .disabled("Z"), .enable("false")) multiplexer_6 (
    .in0(ID_EX_r1_2), .in1(RDin), .in2(MEM_aluResult), .out(multiplexer_6_out), .sel(ID_EX_rs1_forward_2));  // open: in3
  assign CLK = nand_1_out ? clock_2_out : 1'bz;  // Controlled_Buffer controlled_buffer_1
  Multiplexer #(.select(2), .width(32), .disabled("Z"), .enable("false")) multiplexer_7 (
    .in0(ID_EX_r2_2), .in1(RDin), .in2(MEM_aluResult), .out(multiplexer_7_out), .sel(ID_EX_rs2_forward_2));  // open: in3
  Pull_Resistor #(.pull(1)) pull_resistor_1 (.node(CLK));
  Multiplexer #(.select(1), .width(32), .disabled("Z"), .enable("false")) multiplexer_8 (
    .in0(multiplexer_7_out), .in1(ID_EX_imm_1_2), .out(multiplexer_8_out), .sel(ID_EX_alusrcb_2));
  Shifter #(.width(32), .shift("ll")) shifter_1 (.in(ID_EX_imm_2_2), .\dist (5'b00001), .out(shifter_1_out));
  Comparator #(.width(32), .mode("twosComplement")) comparator_2 (
    .a(multiplexer_6_out), .b(32'ha), .eq(comparator_2_eq));  // open: gt, lt
  not not_5 (not_5_out, halt);
  or or_2 (ID_EX_jalr_2[1], and_3_out, ID_EX_jal_2, and_4_out, and_6_out);
  and and_3 (and_3_out, ID_EX_beq_2, alu_1_equal);
  and and_4 (and_4_out, ID_EX_bne_2, ~alu_1_equal);  // AND_Gate
  ALU alu_1 (
    .X(multiplexer_6_out), .Y(multiplexer_8_out), .AluOP(ID_EX_aluop_2), .Equal(alu_1_equal),
    .Result(alu_1_result), .out_6(alu_1_out_6));  // open: Result_2, out_4
  Adder #(.width(32)) adder_2 (.a(shifter_1_out), .b(EX_PC), .out(branch_addr));  // open: cin, cout
  and and_5 (EX_halt, comparator_2_eq, EX_ecall);
  not not_6 (not_6_out, comparator_2_eq);
  Counter #(.width(16), .max('hffff), .ongoal("wrap"), .trigger("rising"), .behavior("new")) counter_2 (
    .count(not_5_out), .Q(\总周期数 ), .clk(CLK));  // open: load, D, carry, clr, preset, down
  or or_3 (or_3_out, ID_EX_jalr_2[1], ID_EX_jalr_2[0]);
  and and_6 (and_6_out, alu_1_out_6, ID_EX_bltu_2);
  Multiplexer #(.select(1), .width(32), .disabled("Z"), .enable("false")) multiplexer_9 (
    .in0(alu_1_result), .in1({EX_IR[31:12], {12{1'b0}}}), .out(ALU_addr), .sel(ID_EX_lui_2));
  Register #(.width(32), .trigger("rising"), .Select("low")) PC_2 (
    .D(multiplexer_7_out), .en(and_7_out), .Q(LedData), .clk(CLK));  // open: clr
  and and_7 (and_7_out, not_6_out, EX_ecall);
  EX_MEM EX_MEM (
    .JAL(ID_EX_jal_2), .Jalr(ID_EX_jalr_2[0]), .MemToReg(ID_EX_memtoreg_2), .MemWrite(ID_EX_memwrite_2),
    .RegWrite(ID_EX_regwrite_2), .halt(EX_halt), .rd(ID_EX_rd_2), .result(ALU_addr),
    .WriteData(multiplexer_7_out), .IR(EX_IR), .PC(EX_PC), .PC_4(ID_EX_pc_4_2), .JAL_2(EX_MEM_jal_2),
    .Jalr_2(EX_MEM_jalr_2), .MemToReg_2(EX_MEM_memtoreg_2), .MemWrite_2(MemWrite),
    .RegWrite_2(EX_MEM_regwrite_2), .halt_2(EX_MEM_halt_2), .rd_2(EX_MEM_rd_2), .result_2(MEM_aluResult),
    .WriteData_2(MDin), .IR_2(MEM_IR), .PC_2(M_PC), .PC_4_2(EX_MEM_pc_4_2), .reset(RST), .en(not_7_out),
    .clk(CLK), .LH(ID_EX_lh_2), .LH_2(EX_MEM_lh_2));
  not not_7 (not_7_out, halt);
  RAM #(.addrWidth(10), .dataWidth(32), .bus("separate"), .Select("high")) ram_1 (
    .addr(MEM_aluResult[11:2]), .din(MDin), .data(ram_1_data), .str(MemWrite), .sel(1'b1), .clk(CLK),
    .ld(1'b1), .clr(RST));
  Multiplexer #(.select(1), .width(16), .disabled("Z"), .enable("false")) multiplexer_10 (
    .in0(ram_1_data[15:0]), .in1(ram_1_data[31:16]), .out(multiplexer_10_out), .sel(MEM_aluResult[1]));
  assign bit_extender_5_out = {{16{multiplexer_10_out[15]}}, multiplexer_10_out};  // Bit_Extender bit_extender_5
  MEM_WB MEM_WB (
    .Jal(EX_MEM_jal_2), .Jalr(EX_MEM_jalr_2), .MenToReg(EX_MEM_memtoreg_2), .RegWrite(EX_MEM_regwrite_2),
    .halt(EX_MEM_halt_2), .rd(EX_MEM_rd_2), .ALUResult(MEM_aluResult), .ReadData(multiplexer_11_out),
    .IR(MEM_IR), .PC(M_PC), .PC_4(EX_MEM_pc_4_2), .Jal_2(MEM_WB_jal_2), .Jalr_2(MEM_WB_jalr_2),
    .MemToReg(MEM_WB_memtoreg[0]), .RegWrite_2(RegWrite), .halt_2(MEM_WB_halt_2), .rd_2(WB_rd),
    .ALUResult_2(MEM_WB_aluresult_2), .ReadData_2(MEM_WB_readdata_2), .IR_2(WB_IR), .PC_2(WB_PC),
    .PC_4_2(MEM_WB_pc_4_2), .reset(RST), .en(not_8_out), .clk(CLK));
  Multiplexer #(.select(1), .width(32), .disabled("Z"), .enable("false")) multiplexer_11 (
    .in0(ram_1_data), .in1(bit_extender_5_out), .out(multiplexer_11_out), .sel(EX_MEM_lh_2));
  not not_8 (not_8_out, halt);
  or or_4 (MEM_WB_memtoreg[1], MEM_WB_jal_2, MEM_WB_jalr_2);
  D_Flip_Flop #(.trigger("rising"), .Pre_Clr_Positions("ABOVE_BELOW"), .NegatePresetClear("false"), .enable("true"), .NewFFLayout("true")) d_ff_2 (
    .clk(MEM_WB_halt_2), .D(1'b1), .Q(halt), .en(1'b1), .reset(Go));  // open: Qn, preset
  Multiplexer #(.select(2), .width(32), .disabled("Z"), .enable("false")) multiplexer_12 (
    .in0(MEM_WB_aluresult_2), .in1(MEM_WB_readdata_2), .in2(MEM_WB_pc_4_2), .out(RDin), .sel(MEM_WB_memtoreg));  // open: in3

  // Other names for the same wires on the sheet: MEM_PC[31:0] = M_PC; WB_RegWrite = RegWrite

  // Notes on the sheet:
  //   中断源
  //   时空图监测，可删除
  //   中断等待指示
  //   数码管输出
  //   IF 阶段
  //   contents of 指令存储器 (hex, n*v repeats v):
  //   100493 100006f 100493 200913 300993 100006f 100493 200913 300993 100006f 100493 200913 300993
  //   100006f 100493 200913 300993 3e4000ef 100413 100493 1f49493 900533 2200893 73 24d493 48463 fedff06f
  //   900533 2200893 73 100493 249493 900533 2200893 73 48463 fedff06f 100493 1f49493 900533 2200893 73
  //   4034d493 900533 2200893 73 4044d493 900533 2200893 73 4044d493 900533 2200893 73 4044d493 900533
  //   2200893 73 4044d493 900533 2200893 73 4044d493 900533 2200893 73 4044d493 900533 2200893 73 4044d493
  //   900533 2200893 73 100413 1f41993 41f9d993 433 c00913 300b13 140413 f47413 800293 100313 499993
  //   89e9b3 1300533 2200893 73 406282b3 fe0294e3 140413 f00f93 1f47433 1c41413 800293 100313 49d993
  //   89e9b3 1300533 2200893 73 406282b3 fe0294e3 1c45413 406b0b33 b0463 f95ff06f 2b3 fff2c293 829293
  //   ff2e293 500533 2200893 73 fff00413 493 84a023 140413 448493 84a023 140413 448493 84a023 140413
  //   448493 84a023 140413 448493 84a023 140413 448493 84a023 140413 448493 84a023 140413 448493 84a023
  //   140413 448493 84a023 140413 448493 84a023 140413 448493 84a023 140413 448493 84a023 140413 448493
  //   84a023 140413 448493 84a023 140413 448493 84a023 140413 448493 84a023 140413 448493 140413 433
  //   3c00493 42983 4aa03 149a2b3 28663 134a023 1442023 ffc48493 fe9412e3 800533 2200893 73 440413 3c00493
  //   fc9416e3 a00893 73 fff00293 7700493 849493 7748493 900533 2200893 73 1000e13 54c4b3 900533 2200893
  //   73 fffe0e13 fe0e16e3 a00893 73 800e13 fedc04b7 fff00413 1045413 84e4b3 900533 2200893 73 ba9804b7
  //   900533 73 765404b7 900533 73 321004b7 900533 73 fffe0e13 fa0e1ee3 a00893 73 313 1000e13 8400493
  //   849493 8348493 400913 891913 490913 849493 8248493 849493 8148493 891913 490913 891913 490913 932023
  //   12484b3 430313 fffe0e13 fe0e18e3 2000e13 313 31483 900533 2200893 73 230313 fffe0e13 fe0e14e3 a00893
  //   73 ff100493 900533 2200893 73 148493 fe9068e3 900533 2200893 73 a00893 73 a00893 73 413 140413
  //   800533 2200893 73 240413 800533 2200893 73 340413 800533 2200893 73 440413 800533 2200893 73 540413
  //   800533 2200893 73 640413 800533 2200893 73 740413 800533 2200893 73 840413 800533 2200893 2200893 73
  //   8067
  //   rs1-used
  //   JAL
  //   Jalr
  //   XOR
  //   LUI
  //   LH
  //   BLTU
  //   rs1
  //   rs2
  //   imm12
  //   imm_sw
  //   rd
  //   ecall
  //   rs2-used
  //   Beq
  //   Bne
  //   MemToReg
  //   MemWrite
  //   AluOP
  //   AluSrcB
  //   RegWrite
  //   Stype
  //   ecall
  //   imm_b
  //   imm_j
  //   ID 阶段
  //   JAL
  //   Jalr
  //   LUI
  //   LH
  //   BLTU
  //   控制位
  //   流水调试日志用
  //   暂停节拍，不能为0
  //   Beq
  //   Bne
  //   AluOP
  //   Stype
  //   戳工具置1进入计数暂停模式，ctrl+k时钟自动运行到对应节拍暂停
  //   ctrl+k关闭时钟连续运行，将控制位置零，进入单步调试模式调试
  //   JAL
  //   Jalr
  //   MemToReg
  //   MemWrite
  //   LUI
  //   AluSrcB
  //   BLTU
  //   RegWrite
  //   可计数暂停的时钟源
  //   EX 阶段
  //   LUI 指令支持电路
  //   为方便自动评测，需要输出流水线各段保存的PC值，注意是PC不是PC+4，另外ID段寄存器写入信息，Mem段内存写入信息也要输出
  //   MemToReg
  //   MemWrite
  //   RegWrite
  //   halt
  //   ALUResult
  //   R2
  //   JAL
  //   Jalr
  //   MEM 阶段
  //   LH 指令支持电路
  //   WB 阶段
  //   JAL
  //   Jalr
  //   MemToReg
  //   ALUResult
  //   MemDataOut
  //   WB.PC+4
endmodule

module \中断按键参考电路  (
  input  \同步清零信号 ,
  output \与中断屏蔽位与 
);

  wire \_1号中断_out , and_1_out, clock_1_out, d_ff_1_q, or_1_out, or_2_out;

  Clock #(.highDuration(1), .lowDuration(1)) clock_1 (.out(clock_1_out));
  Button \_1号中断  (.out(\_1号中断_out ));
  LED #(.active("true")) \_1号中断等待指示灯  (.in(or_1_out));
  or or_1 (or_1_out, \与中断屏蔽位与 , d_ff_1_q);
  D_Flip_Flop #(.trigger("rising"), .Pre_Clr_Positions("LEGACY"), .NegatePresetClear("false"), .enable("true"), .NewFFLayout("false")) d_ff_1 (
    .clk(\_1号中断_out ), .D(1'b1), .Q(d_ff_1_q), .reset(\与中断屏蔽位与 ));  // open: Qn, preset, en
  or or_2 (or_2_out, d_ff_1_q, \与中断屏蔽位与 );
  and and_1 (and_1_out, or_2_out, ~\同步清零信号 );  // AND_Gate
  D_Flip_Flop #(.trigger("rising"), .Pre_Clr_Positions("LEGACY"), .NegatePresetClear("false"), .enable("true"), .NewFFLayout("false")) IR1 (
    .clk(clock_1_out), .D(and_1_out), .Q(\与中断屏蔽位与 ));  // open: Qn, preset, en, reset

  // Notes on the sheet:
  //   中断信号采样参考电路
  //   Reset 
endmodule

module \单周期_单级中断  (
  input  IR1,
  input  IR2,
  input  IR3,
  output RegWrite,
  output MemWrite,
  output [31:0] PC,
  output [31:0] IR,
  output [31:0] RDin,
  output [31:0] MDin,
  output [31:0] LedData
);

  wire CLK, comparator_1_eq, comparator_2_eq, comparator_3_eq, comparator_4_eq, Go, IR1_t, IR2_t, IR3_t, IRA,
       IRB, IRC, or_1_out, W1, W2, W3;
  wire [15:0] \总周期数 ;

  Clock #(.highDuration(1), .lowDuration(1)) clock_1 (.out(CLK));
  Button _1 ();  // open: out
  Button _2 ();  // open: out
  Button _3 ();  // open: out
  Button \u_继续运行  (.out(Go));
  LED #(.active("true")) led_1 (.in(W1));
  LED #(.active("true")) led_2 (.in(W2));
  LED #(.active("true")) led_3 (.in(W3));
  Hex_Digit_Display hex_digit_display_1 (.value(LedData[31:28]));  // open: dp
  Comparator #(.width(16), .mode("twosComplement")) comparator_1 (
    .a(16'h23b), .b(\总周期数 ), .eq(comparator_1_eq));  // open: gt, lt
  Comparator #(.width(16), .mode("twosComplement")) comparator_2 (
    .a(\总周期数 ), .b(16'h1), .eq(comparator_2_eq));  // open: gt, lt
  Comparator #(.width(16), .mode("twosComplement")) comparator_3 (
    .a(\总周期数 ), .b(16'h4), .eq(comparator_3_eq));  // open: gt, lt
  Comparator #(.width(16), .mode("twosComplement")) comparator_4 (
    .a(\总周期数 ), .b(16'h7), .eq(comparator_4_eq));  // open: gt, lt
  Hex_Digit_Display hex_digit_display_2 (.value(LedData[23:20]));  // open: dp
  Hex_Digit_Display hex_digit_display_3 (.value(LedData[27:24]));  // open: dp
  or or_1 (or_1_out, comparator_1_eq, comparator_2_eq);
  assign IRA = or_1_out ? ~CLK : 1'bz;  // Controlled_Inverter controlled_inverter_1
  assign IRB = comparator_3_eq ? ~CLK : 1'bz;  // Controlled_Inverter controlled_inverter_2
  assign IRC = comparator_4_eq ? ~CLK : 1'bz;  // Controlled_Inverter controlled_inverter_3
  Hex_Digit_Display hex_digit_display_4 (.value(LedData[15:12]));  // open: dp
  Hex_Digit_Display hex_digit_display_5 (.value(LedData[19:16]));  // open: dp
  Pull_Resistor #(.pull(0)) pull_resistor_1 (.node(IRA));
  Pull_Resistor #(.pull(0)) pull_resistor_2 (.node(IRB));
  Pull_Resistor #(.pull(0)) pull_resistor_3 (.node(IRC));
  Hex_Digit_Display hex_digit_display_6 (.value(LedData[11:8]));  // open: dp
  Hex_Digit_Display hex_digit_display_7 (.value(LedData[7:4]));  // open: dp
  // Probe on \总周期数 
  Hex_Digit_Display hex_digit_display_8 (.value(LedData[3:0]));  // open: dp
  or or_2 (IR1_t, IR1, IRA);
  or or_3 (IR2_t, IR2, IRB);
  or or_4 (IR3_t, IR3, IRC);

  // Notes on the sheet:
  //   中断源
  //   中断等待指示
  //   总复位信号应将除ROM以外所有存储组件全部清零
  //   单级中断测试信号模拟器
  //   数码管输出
  //   数码管输出应该用寄存器锁存，否则显示数据只能一闪而过
  //   为方便自动评测，需要输出PC，IR，寄存器堆写如数据RDin
  //   RAM写使能MemWrite、RAM写入数据MDin等信号
endmodule

module \单周期_多级中断  (
  input  IR1,
  input  IR2,
  input  IR3,
  output RegWrite,
  output MemWrite,
  output [31:0] PC,
  output [31:0] IR,
  output [31:0] RDin,
  output [31:0] MDin,
  output [31:0] LedData
);

  wire CLK, comparator_1_eq, comparator_2_eq, comparator_3_eq, comparator_4_eq, comparator_5_eq, Go, IR1_t,
       IR2_t, IR3_t, IRA, IRB, IRC, or_1_out, or_2_out, W1, W2, W3;
  wire [15:0] \总周期数 ;

  Clock #(.highDuration(1), .lowDuration(1)) clock_1 (.out(CLK));
  Button _1 ();  // open: out
  Button _2 ();  // open: out
  Button _3 ();  // open: out
  Button \u_继续运行  (.out(Go));
  LED #(.active("true")) led_1 (.in(W1));
  LED #(.active("true")) led_2 (.in(W2));
  LED #(.active("true")) led_3 (.in(W3));
  Hex_Digit_Display hex_digit_display_1 (.value(LedData[31:28]));  // open: dp
  Comparator #(.width(16), .mode("twosComplement")) comparator_1 (
    .a(\总周期数 ), .b(16'h7), .eq(comparator_1_eq));  // open: gt, lt
  Comparator #(.width(16), .mode("twosComplement")) comparator_2 (
    .a(\总周期数 ), .b(16'h241), .eq(comparator_2_eq));  // open: gt, lt
  Hex_Digit_Display hex_digit_display_2 (.value(LedData[23:20]));  // open: dp
  Hex_Digit_Display hex_digit_display_3 (.value(LedData[27:24]));  // open: dp
  Comparator #(.width(16), .mode("twosComplement")) comparator_3 (
    .a(16'h258), .b(\总周期数 ), .eq(comparator_3_eq));  // open: gt, lt
  or or_1 (or_1_out, comparator_3_eq, comparator_4_eq);
  Comparator #(.width(16), .mode("twosComplement")) comparator_4 (
    .a(\总周期数 ), .b(16'h1), .eq(comparator_4_eq));  // open: gt, lt
  Comparator #(.width(16), .mode("twosComplement")) comparator_5 (
    .a(\总周期数 ), .b(16'h4), .eq(comparator_5_eq));  // open: gt, lt
  or or_2 (or_2_out, comparator_1_eq, comparator_2_eq);
  Hex_Digit_Display hex_digit_display_4 (.value(LedData[19:16]));  // open: dp
  Hex_Digit_Display hex_digit_display_5 (.value(LedData[15:12]));  // open: dp
  Pull_Resistor #(.pull(0)) pull_resistor_1 (.node(IRA));
  assign IRA = or_1_out ? ~CLK : 1'bz;  // Controlled_Inverter controlled_inverter_1
  Pull_Resistor #(.pull(0)) pull_resistor_2 (.node(IRB));
  assign IRB = comparator_5_eq ? ~CLK : 1'bz;  // Controlled_Inverter controlled_inverter_2
  Pull_Resistor #(.pull(0)) pull_resistor_3 (.node(IRC));
  assign IRC = or_2_out ? ~CLK : 1'bz;  // Controlled_Inverter controlled_inverter_3
  Hex_Digit_Display hex_digit_display_6 (.value(LedData[11:8]));  // open: dp
  Hex_Digit_Display hex_digit_display_7 (.value(LedData[7:4]));  // open: dp
  // Probe on \总周期数 
  Hex_Digit_Display hex_digit_display_8 (.value(LedData[3:0]));  // open: dp
  or or_3 (IR1_t, IR1, IRA);
  or or_4 (IR2_t, IR2, IRB);
  or or_5 (IR3_t, IR3, IRC);

  // Notes on the sheet:
  //   中断源
  //   中断等待指示
  //   总复位信号应将除ROM以外所有存储组件全部清零
  //   多级中断测试信号模拟器
  //   数码管输出
  //   数码管输出应该用寄存器锁存，否则显示数据只能一闪而过
  //   为方便自动评测，需要输出PC，IR，寄存器堆写如数据RDin
  //   RAM写使能MemWrite、RAM写入数据MDin等信号
endmodule

module \封装正确性测试  (
);

  wire IR1, IR2, IR3, MemW, RegW;
  wire [31:0] EX_PC, ID_PC, IF_PC, IR, LED, MDin, MDinr, MEM_PC, PC, RDin, RDinr, WB_PC;

  \单周期RISC_V  \u_单周期risc_v_1  (
    .IR1(IR1), .IR2(IR2), .IR3(IR3), .RegWrite(RegW), .MemWrite(MemW), .PC(PC), .IR(IR), .RDin(RDin),
    .MDin(MDin), .LedData(LED));
  \气泡流水线  \u_气泡流水线_1  (
    .RegWrite(RegW), .MemWrite(MemW), .IF_PC(IF_PC), .ID_PC(ID_PC), .EX_PC(EX_PC), .M_PC(MEM_PC),
    .WB_PC(WB_PC), .RDin(RDinr), .MDin(MDinr), .LedData(LED));
  \单周期_单级中断  \u_单周期_单级中断_1  (
    .IR1(IR1), .IR2(IR2), .IR3(IR3), .RegWrite(RegW), .MemWrite(MemW), .PC(PC), .IR(IR), .RDin(RDin),
    .MDin(MDin), .LedData(LED));
  \理想流水线  \u_理想流水线_1  (
    .RegWrite(RegW), .MemWrite(MemW), .IF_PC(IF_PC), .ID_PC(ID_PC), .EX_PC(EX_PC), .M_PC(MEM_PC),
    .WB_PC(WB_PC), .RDin(RDinr), .MDin(MDinr), .LedData(LED));
  \重定向流水线  \u_重定向流水线_1  (
    .RegWrite(RegW), .MemWrite(MemW), .IF_PC(IF_PC), .ID_PC(ID_PC), .EX_PC(EX_PC), .M_PC(MEM_PC),
    .WB_PC(WB_PC), .RDin(RDinr), .MDin(MDinr), .LedData(LED));
  \单周期_多级中断  \u_单周期_多级中断_1  (
    .IR1(IR1), .IR2(IR2), .IR3(IR3), .RegWrite(RegW), .MemWrite(MemW), .PC(PC), .IR(IR), .RDin(RDin),
    .MDin(MDin), .LedData(LED));

  // Notes on the sheet:
  //   单周期封装测试
  //   气泡流水封装测试
  //   单周期+单级中断封装测试
  //   请检查上面封装有无位宽不匹配，引脚标签是否和连接的标签相对应，否则无法在educoder平台上正确测试
  //   理想流水封装测试
  //   重定向流水封装测试
  //   单周期+多级中断封装测试
endmodule

module ID_EX (
  input  Beq,
  input  Bne,
  input  MemToReg,
  input  MemWrite,
  input  AluSrcB,
  input  RegWrite,
  input  SType,
  input  ecall,
  input  Jal,
  input  Jalr,
  input  LUI,
  input  LH,
  input  BLTU,
  input  [3:0] AluOP,
  input  [4:0] rd,
  input  [31:0] R1,
  input  [31:0] R2,
  input  [31:0] imm_1,
  input  [31:0] imm_2,
  input  [31:0] PC,
  input  [31:0] PC_4,
  input  [31:0] IR,
  input  [1:0] RS1_Forward,
  input  [1:0] RS2_Forward,
  input  en,
  input  clk,
  input  reset,
  input  flush,
  output Beq_2,
  output Bne_2,
  output MemToReg_2,
  output MemWrite_2,
  output AluSrcB_2,
  output RegWrite_2,
  output SType_2,
  output ecall_2,
  output Jal_2,
  output Jalr_2,
  output LUI_2,
  output LH_2,
  output BLTU_2,
  output [3:0] AluOP_2,
  output [4:0] rd_2,
  output [31:0] R1_2,
  output [31:0] R2_2,
  output [31:0] imm_1_2,
  output [31:0] imm_2_2,
  output [31:0] PC_2,
  output [31:0] PC_4_2,
  output [31:0] IR_2,
  output [1:0] RS1_Forward_2,
  output [1:0] RS2_Forward_2
);

  wire multiplexer_1_out, multiplexer_2_out, multiplexer_3_out, multiplexer_4_out, multiplexer_5_out,
       multiplexer_6_out, multiplexer_7_out, multiplexer_8_out, multiplexer_9_out, multiplexer_10_out,
       multiplexer_11_out, multiplexer_12_out, multiplexer_13_out, or_1_out;
  wire [1:0] multiplexer_23_out, multiplexer_24_out;
  wire [3:0] multiplexer_14_out;
  wire [4:0] multiplexer_15_out;
  wire [31:0] multiplexer_16_out, multiplexer_17_out, multiplexer_18_out, multiplexer_19_out,
       multiplexer_20_out, multiplexer_21_out, multiplexer_22_out;

  Multiplexer #(.select(1), .width(1), .disabled("Z"), .enable("false")) multiplexer_1 (
    .in0(Beq), .in1(1'b0), .out(multiplexer_1_out), .sel(or_1_out));
  Multiplexer #(.select(1), .width(1), .disabled("Z"), .enable("false")) multiplexer_2 (
    .in0(Bne), .in1(1'b0), .out(multiplexer_2_out), .sel(or_1_out));
  Multiplexer #(.select(1), .width(1), .disabled("Z"), .enable("false")) multiplexer_3 (
    .in0(MemToReg), .in1(1'b0), .out(multiplexer_3_out), .sel(or_1_out));
  Multiplexer #(.select(1), .width(1), .disabled("Z"), .enable("false")) multiplexer_4 (
    .in0(MemWrite), .in1(1'b0), .out(multiplexer_4_out), .sel(or_1_out));
  Multiplexer #(.select(1), .width(1), .disabled("Z"), .enable("false")) multiplexer_5 (
    .in0(AluSrcB), .in1(1'b0), .out(multiplexer_5_out), .sel(or_1_out));
  Multiplexer #(.select(1), .width(1), .disabled("Z"), .enable("false")) multiplexer_6 (
    .in0(RegWrite), .in1(1'b0), .out(multiplexer_6_out), .sel(or_1_out));
  Multiplexer #(.select(1), .width(1), .disabled("Z"), .enable("false")) multiplexer_7 (
    .in0(SType), .in1(1'b0), .out(multiplexer_7_out), .sel(or_1_out));
  Multiplexer #(.select(1), .width(1), .disabled("Z"), .enable("false")) multiplexer_8 (
    .in0(ecall), .in1(1'b0), .out(multiplexer_8_out), .sel(or_1_out));
  Multiplexer #(.select(1), .width(1), .disabled("Z"), .enable("false")) multiplexer_9 (
    .in0(Jal), .in1(1'b0), .out(multiplexer_9_out), .sel(or_1_out));
  Multiplexer #(.select(1), .width(1), .disabled("Z"), .enable("false")) multiplexer_10 (
    .in0(Jalr), .in1(1'b0), .out(multiplexer_10_out), .sel(or_1_out));
  Multiplexer #(.select(1), .width(1), .disabled("Z"), .enable("false")) multiplexer_11 (
    .in0(LUI), .in1(1'b0), .out(multiplexer_11_out), .sel(or_1_out));
  Multiplexer #(.select(1), .width(1), .disabled("Z"), .enable("false")) multiplexer_12 (
    .in0(LH), .in1(1'b0), .out(multiplexer_12_out), .sel(or_1_out));
  Multiplexer #(.select(1), .width(1), .disabled("Z"), .enable("false")) multiplexer_13 (
    .in0(BLTU), .in1(1'b0), .out(multiplexer_13_out), .sel(or_1_out));
  Multiplexer #(.select(1), .width(4), .disabled("Z"), .enable("false")) multiplexer_14 (
    .in0(AluOP), .in1(4'b0000), .out(multiplexer_14_out), .sel(or_1_out));
  Multiplexer #(.select(1), .width(5), .disabled("Z"), .enable("false")) multiplexer_15 (
    .in0(rd), .in1({5{1'b0}}), .out(multiplexer_15_out), .sel(or_1_out));
  Multiplexer #(.select(1), .width(32), .disabled("Z"), .enable("false")) multiplexer_16 (
    .in0(R1), .in1({32{1'b0}}), .out(multiplexer_16_out), .sel(or_1_out));
  Multiplexer #(.select(1), .width(32), .disabled("Z"), .enable("false")) multiplexer_17 (
    .in0(R2), .in1({32{1'b0}}), .out(multiplexer_17_out), .sel(or_1_out));
  Multiplexer #(.select(1), .width(32), .disabled("Z"), .enable("false")) multiplexer_18 (
    .in0(imm_1), .in1({32{1'b0}}), .out(multiplexer_18_out), .sel(or_1_out));
  Multiplexer #(.select(1), .width(32), .disabled("Z"), .enable("false")) multiplexer_19 (
    .in0(imm_2), .in1({32{1'b0}}), .out(multiplexer_19_out), .sel(or_1_out));
  Multiplexer #(.select(1), .width(32), .disabled("Z"), .enable("false")) multiplexer_20 (
    .in0(PC), .in1({32{1'b0}}), .out(multiplexer_20_out), .sel(or_1_out));
  Multiplexer #(.select(1), .width(32), .disabled("Z"), .enable("false")) multiplexer_21 (
    .in0(PC_4), .in1({32{1'b0}}), .out(multiplexer_21_out), .sel(or_1_out));
  Multiplexer #(.select(1), .width(32), .disabled("Z"), .enable("false")) multiplexer_22 (
    .in0(IR), .in1({32{1'b0}}), .out(multiplexer_22_out), .sel(or_1_out));
  Multiplexer #(.select(1), .width(2), .disabled("Z"), .enable("false")) multiplexer_23 (
    .in0(RS1_Forward), .in1(2'b00), .out(multiplexer_23_out), .sel(or_1_out));
  Multiplexer #(.select(1), .width(2), .disabled("Z"), .enable("false")) multiplexer_24 (
    .in0(RS2_Forward), .in1(2'b00), .out(multiplexer_24_out), .sel(or_1_out));
  or or_1 (or_1_out, reset, flush);
  Register #(.width(1), .trigger("rising"), .Select("low")) register_1 (
    .D(multiplexer_1_out), .en(en), .Q(Beq_2), .clk(clk));  // open: clr
  Register #(.width(1), .trigger("rising"), .Select("low")) register_2 (
    .D(multiplexer_2_out), .en(en), .Q(Bne_2), .clk(clk));  // open: clr
  Register #(.width(1), .trigger("rising"), .Select("low")) register_3 (
    .D(multiplexer_3_out), .en(en), .Q(MemToReg_2), .clk(clk));  // open: clr
  Register #(.width(1), .trigger("rising"), .Select("low")) register_4 (
    .D(multiplexer_4_out), .en(en), .Q(MemWrite_2), .clk(clk));  // open: clr
  Register #(.width(1), .trigger("rising"), .Select("low")) register_5 (
    .D(multiplexer_5_out), .en(en), .Q(AluSrcB_2), .clk(clk));  // open: clr
  Register #(.width(1), .trigger("rising"), .Select("low")) register_6 (
    .D(multiplexer_6_out), .en(en), .Q(RegWrite_2), .clk(clk));  // open: clr
  Register #(.width(1), .trigger("rising"), .Select("low")) register_7 (
    .D(multiplexer_7_out), .en(en), .Q(SType_2), .clk(clk));  // open: clr
  Register #(.width(1), .trigger("rising"), .Select("low")) register_8 (
    .D(multiplexer_8_out), .en(en), .Q(ecall_2), .clk(clk));  // open: clr
  Register #(.width(1), .trigger("rising"), .Select("low")) register_9 (
    .D(multiplexer_9_out), .en(en), .Q(Jal_2), .clk(clk));  // open: clr
  Register #(.width(1), .trigger("rising"), .Select("low")) register_10 (
    .D(multiplexer_10_out), .en(en), .Q(Jalr_2), .clk(clk));  // open: clr
  Register #(.width(1), .trigger("rising"), .Select("low")) register_11 (
    .D(multiplexer_11_out), .en(en), .Q(LUI_2), .clk(clk));  // open: clr
  Register #(.width(1), .trigger("rising"), .Select("low")) register_12 (
    .D(multiplexer_12_out), .en(en), .Q(LH_2), .clk(clk));  // open: clr
  Register #(.width(1), .trigger("rising"), .Select("low")) register_13 (
    .D(multiplexer_13_out), .en(en), .Q(BLTU_2), .clk(clk));  // open: clr
  Register #(.width(4), .trigger("rising"), .Select("low")) register_14 (
    .D(multiplexer_14_out), .en(en), .Q(AluOP_2), .clk(clk));  // open: clr
  Register #(.width(5), .trigger("rising"), .Select("low")) register_15 (
    .D(multiplexer_15_out), .en(en), .Q(rd_2), .clk(clk));  // open: clr
  Register #(.width(32), .trigger("rising"), .Select("low")) register_16 (
    .D(multiplexer_16_out), .en(en), .Q(R1_2), .clk(clk));  // open: clr
  Register #(.width(32), .trigger("rising"), .Select("low")) register_17 (
    .D(multiplexer_17_out), .en(en), .Q(R2_2), .clk(clk));  // open: clr
  Register #(.width(32), .trigger("rising"), .Select("low")) register_18 (
    .D(multiplexer_18_out), .en(en), .Q(imm_1_2), .clk(clk));  // open: clr
  Register #(.width(32), .trigger("rising"), .Select("low")) register_19 (
    .D(multiplexer_19_out), .en(en), .Q(imm_2_2), .clk(clk));  // open: clr
  Register #(.width(32), .trigger("rising"), .Select("low")) register_20 (
    .D(multiplexer_20_out), .en(en), .Q(PC_2), .clk(clk));  // open: clr
  Register #(.width(32), .trigger("rising"), .Select("low")) register_21 (
    .D(multiplexer_21_out), .en(en), .Q(PC_4_2), .clk(clk));  // open: clr
  Register #(.width(32), .trigger("rising"), .Select("low")) register_22 (
    .D(multiplexer_22_out), .en(en), .Q(IR_2), .clk(clk));  // open: clr
  Register #(.width(2), .trigger("rising"), .Select("low")) register_23 (
    .D(multiplexer_23_out), .en(en), .Q(RS1_Forward_2), .clk(clk));  // open: clr
  Register #(.width(2), .trigger("rising"), .Select("low")) register_24 (
    .D(multiplexer_24_out), .en(en), .Q(RS2_Forward_2), .clk(clk));  // open: clr
endmodule

module IF_ID (
  input  [31:0] IR,
  input  [31:0] PC,
  input  [31:0] PC_4,
  input  en,
  input  clk,
  input  reset,
  input  BranchTaken,
  output [31:0] IR_2,
  output [31:0] PC_2,
  output [31:0] PC_4_2
);

  wire or_1_out;
  wire [31:0] multiplexer_1_out, multiplexer_2_out, multiplexer_3_out;

  Multiplexer #(.select(1), .width(32), .disabled("Z"), .enable("false")) multiplexer_1 (
    .in0(IR), .in1({32{1'b0}}), .out(multiplexer_1_out), .sel(or_1_out));
  Multiplexer #(.select(1), .width(32), .disabled("Z"), .enable("false")) multiplexer_2 (
    .in0(PC), .in1({32{1'b0}}), .out(multiplexer_2_out), .sel(or_1_out));
  Multiplexer #(.select(1), .width(32), .disabled("Z"), .enable("false")) multiplexer_3 (
    .in0(PC_4), .in1({32{1'b0}}), .out(multiplexer_3_out), .sel(or_1_out));
  or or_1 (or_1_out, reset, BranchTaken);
  Register #(.width(32), .trigger("rising"), .Select("low")) register_1 (
    .D(multiplexer_1_out), .en(en), .Q(IR_2), .clk(clk));  // open: clr
  Register #(.width(32), .trigger("rising"), .Select("low")) register_2 (
    .D(multiplexer_2_out), .en(en), .Q(PC_2), .clk(clk));  // open: clr
  Register #(.width(32), .trigger("rising"), .Select("low")) register_3 (
    .D(multiplexer_3_out), .en(en), .Q(PC_4_2), .clk(clk));  // open: clr
endmodule

module EX_MEM (
  input  JAL,
  input  Jalr,
  input  MemToReg,
  input  MemWrite,
  input  LH,
  input  RegWrite,
  input  halt,
  input  [4:0] rd,
  input  [31:0] result,
  input  [31:0] WriteData,
  input  [31:0] IR,
  input  [31:0] PC,
  input  [31:0] PC_4,
  input  reset,
  input  en,
  input  clk,
  output JAL_2,
  output Jalr_2,
  output MemToReg_2,
  output MemWrite_2,
  output LH_2,
  output RegWrite_2,
  output halt_2,
  output [4:0] rd_2,
  output [31:0] result_2,
  output [31:0] WriteData_2,
  output [31:0] IR_2,
  output [31:0] PC_2,
  output [31:0] PC_4_2
);

  wire multiplexer_1_out, multiplexer_2_out, multiplexer_3_out, multiplexer_4_out, multiplexer_5_out,
       multiplexer_6_out, multiplexer_7_out;
  wire [4:0] multiplexer_8_out;
  wire [31:0] multiplexer_9_out, multiplexer_10_out, multiplexer_11_out, multiplexer_12_out,
       multiplexer_13_out;

  Multiplexer #(.select(1), .width(1), .disabled("Z"), .enable("false")) multiplexer_1 (
    .in0(JAL), .in1(1'b0), .out(multiplexer_1_out), .sel(reset));
  Multiplexer #(.select(1), .width(1), .disabled("Z"), .enable("false")) multiplexer_2 (
    .in0(Jalr), .in1(1'b0), .out(multiplexer_2_out), .sel(reset));
  Multiplexer #(.select(1), .width(1), .disabled("Z"), .enable("false")) multiplexer_3 (
    .in0(MemToReg), .in1(1'b0), .out(multiplexer_3_out), .sel(reset));
  Multiplexer #(.select(1), .width(1), .disabled("Z"), .enable("false")) multiplexer_4 (
    .in0(MemWrite), .in1(1'b0), .out(multiplexer_4_out), .sel(reset));
  Multiplexer #(.select(1), .width(1), .disabled("Z"), .enable("false")) multiplexer_5 (
    .in0(LH), .in1(1'b0), .out(multiplexer_5_out), .sel(reset));
  Multiplexer #(.select(1), .width(1), .disabled("Z"), .enable("false")) multiplexer_6 (
    .in0(RegWrite), .in1(1'b0), .out(multiplexer_6_out), .sel(reset));
  Multiplexer #(.select(1), .width(1), .disabled("Z"), .enable("false")) multiplexer_7 (
    .in0(halt), .in1(1'b0), .out(multiplexer_7_out), .sel(reset));
  Multiplexer #(.select(1), .width(5), .disabled("Z"), .enable("false")) multiplexer_8 (
    .in0(rd), .in1({5{1'b0}}), .out(multiplexer_8_out), .sel(reset));
  Multiplexer #(.select(1), .width(32), .disabled("Z"), .enable("false")) multiplexer_9 (
    .in0(result), .in1({32{1'b0}}), .out(multiplexer_9_out), .sel(reset));
  Multiplexer #(.select(1), .width(32), .disabled("Z"), .enable("false")) multiplexer_10 (
    .in0(WriteData), .in1({32{1'b0}}), .out(multiplexer_10_out), .sel(reset));
  Multiplexer #(.select(1), .width(32), .disabled("Z"), .enable("false")) multiplexer_11 (
    .in0(IR), .in1({32{1'b0}}), .out(multiplexer_11_out), .sel(reset));
  Multiplexer #(.select(1), .width(32), .disabled("Z"), .enable("false")) multiplexer_12 (
    .in0(PC), .in1({32{1'b0}}), .out(multiplexer_12_out), .sel(reset));
  Multiplexer #(.select(1), .width(32), .disabled("Z"), .enable("false")) multiplexer_13 (
    .in0(PC_4), .in1({32{1'b0}}), .out(multiplexer_13_out), .sel(reset));
  Register #(.width(1), .trigger("rising"), .Select("low")) register_1 (
    .D(multiplexer_1_out), .en(en), .Q(JAL_2), .clk(clk));  // open: clr
  Register #(.width(1), .trigger("rising"), .Select("low")) register_2 (
    .D(multiplexer_2_out), .en(en), .Q(Jalr_2), .clk(clk));  // open: clr
  Register #(.width(1), .trigger("rising"), .Select("low")) register_3 (
    .D(multiplexer_3_out), .en(en), .Q(MemToReg_2), .clk(clk));  // open: clr
  Register #(.width(1), .trigger("rising"), .Select("low")) register_4 (
    .D(multiplexer_4_out), .en(en), .Q(MemWrite_2), .clk(clk));  // open: clr
  Register #(.width(1), .trigger("rising"), .Select("low")) register_5 (
    .D(multiplexer_5_out), .en(en), .Q(LH_2), .clk(clk));  // open: clr
  Register #(.width(1), .trigger("rising"), .Select("low")) register_6 (
    .D(multiplexer_6_out), .en(en), .Q(RegWrite_2), .clk(clk));  // open: clr
  Register #(.width(1), .trigger("rising"), .Select("low")) register_7 (
    .D(multiplexer_7_out), .en(en), .Q(halt_2), .clk(clk));  // open: clr
  Register #(.width(5), .trigger("rising"), .Select("low")) register_8 (
    .D(multiplexer_8_out), .en(en), .Q(rd_2), .clk(clk));  // open: clr
  Register #(.width(32), .trigger("rising"), .Select("low")) register_9 (
    .D(multiplexer_9_out), .en(en), .Q(result_2), .clk(clk));  // open: clr
  Register #(.width(32), .trigger("rising"), .Select("low")) register_10 (
    .D(multiplexer_10_out), .en(en), .Q(WriteData_2), .clk(clk));  // open: clr
  Register #(.width(32), .trigger("rising"), .Select("low")) register_11 (
    .D(multiplexer_11_out), .en(en), .Q(IR_2), .clk(clk));  // open: clr
  Register #(.width(32), .trigger("rising"), .Select("low")) register_12 (
    .D(multiplexer_12_out), .en(en), .Q(PC_2), .clk(clk));  // open: clr
  Register #(.width(32), .trigger("rising"), .Select("low")) register_13 (
    .D(multiplexer_13_out), .en(en), .Q(PC_4_2), .clk(clk));  // open: clr
endmodule

module MEM_WB (
  input  Jal,
  input  Jalr,
  input  MenToReg,
  input  RegWrite,
  input  halt,
  input  [4:0] rd,
  input  [31:0] ALUResult,
  input  [31:0] ReadData,
  input  [31:0] IR,
  input  [31:0] PC,
  input  [31:0] PC_4,
  input  reset,
  input  en,
  input  clk,
  output Jal_2,
  output Jalr_2,
  output MemToReg,
  output RegWrite_2,
  output halt_2,
  output [4:0] rd_2,
  output [31:0] ALUResult_2,
  output [31:0] ReadData_2,
  output [31:0] IR_2,
  output [31:0] PC_2,
  output [31:0] PC_4_2
);

  wire multiplexer_1_out, multiplexer_2_out, multiplexer_3_out, multiplexer_4_out, multiplexer_5_out;
  wire [4:0] multiplexer_6_out;
  wire [31:0] multiplexer_7_out, multiplexer_8_out, multiplexer_9_out, multiplexer_10_out, multiplexer_11_out;

  Multiplexer #(.select(1), .width(1), .disabled("Z"), .enable("false")) multiplexer_1 (
    .in0(Jal), .in1(1'b0), .out(multiplexer_1_out), .sel(reset));
  Multiplexer #(.select(1), .width(1), .disabled("Z"), .enable("false")) multiplexer_2 (
    .in0(Jalr), .in1(1'b0), .out(multiplexer_2_out), .sel(reset));
  Multiplexer #(.select(1), .width(1), .disabled("Z"), .enable("false")) multiplexer_3 (
    .in0(MenToReg), .in1(1'b0), .out(multiplexer_3_out), .sel(reset));
  Multiplexer #(.select(1), .width(1), .disabled("Z"), .enable("false")) multiplexer_4 (
    .in0(RegWrite), .in1(1'b0), .out(multiplexer_4_out), .sel(reset));
  Multiplexer #(.select(1), .width(1), .disabled("Z"), .enable("false")) multiplexer_5 (
    .in0(halt), .in1(1'b0), .out(multiplexer_5_out), .sel(reset));
  Multiplexer #(.select(1), .width(5), .disabled("Z"), .enable("false")) multiplexer_6 (
    .in0(rd), .in1({5{1'b0}}), .out(multiplexer_6_out), .sel(reset));
  Multiplexer #(.select(1), .width(32), .disabled("Z"), .enable("false")) multiplexer_7 (
    .in0(ALUResult), .in1({32{1'b0}}), .out(multiplexer_7_out), .sel(reset));
  Multiplexer #(.select(1), .width(32), .disabled("Z"), .enable("false")) multiplexer_8 (
    .in0(ReadData), .in1({32{1'b0}}), .out(multiplexer_8_out), .sel(reset));
  Multiplexer #(.select(1), .width(32), .disabled("Z"), .enable("false")) multiplexer_9 (
    .in0(IR), .in1({32{1'b0}}), .out(multiplexer_9_out), .sel(reset));
  Multiplexer #(.select(1), .width(32), .disabled("Z"), .enable("false")) multiplexer_10 (
    .in0(PC), .in1({32{1'b0}}), .out(multiplexer_10_out), .sel(reset));
  Multiplexer #(.select(1), .width(32), .disabled("Z"), .enable("false")) multiplexer_11 (
    .in0(PC_4), .in1({32{1'b0}}), .out(multiplexer_11_out), .sel(reset));
  Register #(.width(1), .trigger("rising"), .Select("low")) register_1 (
    .D(multiplexer_1_out), .en(en), .Q(Jal_2), .clk(clk));  // open: clr
  Register #(.width(1), .trigger("rising"), .Select("low")) register_2 (
    .D(multiplexer_2_out), .en(en), .Q(Jalr_2), .clk(clk));  // open: clr
  Register #(.width(1), .trigger("rising"), .Select("low")) register_3 (
    .D(multiplexer_3_out), .en(en), .Q(MemToReg), .clk(clk));  // open: clr
  Register #(.width(1), .trigger("rising"), .Select("low")) register_4 (
    .D(multiplexer_4_out), .en(en), .Q(RegWrite_2), .clk(clk));  // open: clr
  Register #(.width(1), .trigger("rising"), .Select("low")) register_5 (
    .D(multiplexer_5_out), .en(en), .Q(halt_2), .clk(clk));  // open: clr
  Register #(.width(5), .trigger("rising"), .Select("low")) register_6 (
    .D(multiplexer_6_out), .en(en), .Q(rd_2), .clk(clk));  // open: clr
  Register #(.width(32), .trigger("rising"), .Select("low")) register_7 (
    .D(multiplexer_7_out), .en(en), .Q(ALUResult_2), .clk(clk));  // open: clr
  Register #(.width(32), .trigger("rising"), .Select("low")) register_8 (
    .D(multiplexer_8_out), .en(en), .Q(ReadData_2), .clk(clk));  // open: clr
  Register #(.width(32), .trigger("rising"), .Select("low")) register_9 (
    .D(multiplexer_9_out), .en(en), .Q(IR_2), .clk(clk));  // open: clr
  Register #(.width(32), .trigger("rising"), .Select("low")) register_10 (
    .D(multiplexer_10_out), .en(en), .Q(PC_2), .clk(clk));  // open: clr
  Register #(.width(32), .trigger("rising"), .Select("low")) register_11 (
    .D(multiplexer_11_out), .en(en), .Q(PC_4_2), .clk(clk));  // open: clr
endmodule

module \气泡处理逻辑  (
  input  BranchTaken,
  input  [31:0] IR,
  input  ecall,
  input  rs1_used,
  input  EX_RegWrite,
  input  [4:0] EX_rd,
  input  rs2_used,
  input  MEM_RegWrite,
  input  [4:0] MEM_rd,
  output stall,
  output flush
);

  wire and_1_out, and_2_out, and_3_out, and_4_out, and_5_out, and_6_out, and_7_out, and_8_out, and_9_out,
       and_10_out, and_11_out, and_12_out, and_13_out, and_14_out, and_15_out, and_16_out, comparator_1_eq,
       comparator_2_eq, comparator_3_eq, comparator_4_eq, comparator_5_eq, comparator_6_eq, comparator_7_eq,
       comparator_8_eq, comparator_9_eq, comparator_10_eq, comparator_11_eq, comparator_12_eq, not_1_out,
       not_2_out, not_3_out, not_4_out, or_1_out, or_2_out;

  Comparator #(.width(5), .mode("twosComplement")) comparator_1 (
    .a(IR[19:15]), .b(EX_rd), .eq(comparator_1_eq));  // open: gt, lt
  Comparator #(.width(5), .mode("twosComplement")) comparator_2 (
    .a(IR[24:20]), .b(EX_rd), .eq(comparator_2_eq));  // open: gt, lt
  Comparator #(.width(5), .mode("twosComplement")) comparator_3 (
    .a(IR[19:15]), .b(MEM_rd), .eq(comparator_3_eq));  // open: gt, lt
  Comparator #(.width(5), .mode("twosComplement")) comparator_4 (
    .a(IR[24:20]), .b(MEM_rd), .eq(comparator_4_eq));  // open: gt, lt
  Comparator #(.width(5), .mode("twosComplement")) comparator_5 (
    .a({5{1'b0}}), .b(IR[19:15]), .eq(comparator_5_eq));  // open: gt, lt
  not not_1 (not_1_out, comparator_5_eq);
  and and_1 (and_1_out, comparator_1_eq, EX_RegWrite);
  Comparator #(.width(5), .mode("twosComplement")) comparator_6 (
    .a({5{1'b0}}), .b(IR[24:20]), .eq(comparator_6_eq));  // open: gt, lt
  not not_2 (not_2_out, comparator_6_eq);
  and and_2 (and_2_out, comparator_2_eq, EX_RegWrite);
  not not_3 (not_3_out, comparator_7_eq);
  Comparator #(.width(5), .mode("twosComplement")) comparator_7 (
    .a({5{1'b0}}), .b(IR[19:15]), .eq(comparator_7_eq));  // open: gt, lt
  and and_3 (and_3_out, comparator_3_eq, MEM_RegWrite);
  not not_4 (not_4_out, comparator_8_eq);
  Comparator #(.width(5), .mode("twosComplement")) comparator_8 (
    .a({5{1'b0}}), .b(IR[24:20]), .eq(comparator_8_eq));  // open: gt, lt
  and and_4 (and_4_out, comparator_4_eq, MEM_RegWrite);
  Comparator #(.width(5), .mode("twosComplement")) comparator_9 (
    .a(5'b10001), .b(EX_rd), .eq(comparator_9_eq));  // open: gt, lt
  Comparator #(.width(5), .mode("twosComplement")) comparator_10 (
    .a(EX_rd), .b(5'b01010), .eq(comparator_10_eq));  // open: gt, lt
  Comparator #(.width(5), .mode("twosComplement")) comparator_11 (
    .a(5'b10001), .b(MEM_rd), .eq(comparator_11_eq));  // open: gt, lt
  Comparator #(.width(5), .mode("twosComplement")) comparator_12 (
    .a(MEM_rd), .b(5'b01010), .eq(comparator_12_eq));  // open: gt, lt
  and and_5 (and_5_out, not_1_out, and_1_out);
  and and_6 (and_6_out, not_2_out, and_2_out);
  and and_7 (and_7_out, not_3_out, and_3_out);
  and and_8 (and_8_out, not_4_out, and_4_out);
  and and_9 (and_9_out, ecall, EX_RegWrite);
  or or_1 (or_1_out, comparator_9_eq, comparator_10_eq);
  and and_10 (and_10_out, ecall, MEM_RegWrite);
  or or_2 (or_2_out, comparator_11_eq, comparator_12_eq);
  and and_11 (and_11_out, and_5_out, rs1_used);
  and and_12 (and_12_out, and_6_out, rs2_used);
  and and_13 (and_13_out, and_7_out, rs1_used);
  and and_14 (and_14_out, and_8_out, rs2_used);
  and and_15 (and_15_out, and_9_out, or_1_out);
  and and_16 (and_16_out, and_10_out, or_2_out);
  or or_3 (stall, and_11_out, and_12_out, and_13_out, and_14_out, and_15_out, and_16_out);
  or or_4 (flush, stall, BranchTaken);

  // Other names for the same wires on the sheet: data_hazzard = stall; rs1[4:0] = IR[19:15]; rs2[4:0] = IR[24:20]

  // Notes on the sheet:
  //   气泡处理输入(Input)
  //   数据相关检测逻辑
  //   数据相关处理逻辑 & 气泡处理输出(Output)
endmodule

module \重定向处理逻辑  (
  input  BranchTaken,
  input  [31:0] IR,
  input  EX_MemToReg,
  input  ecall,
  input  rs1_used,
  input  EX_RegWrite,
  input  [4:0] EX_rd,
  input  rs2_used,
  input  MEM_RegWrite,
  input  [4:0] MEM_rd,
  output stall,
  output flush,
  output [1:0] rs1Forward,
  output [1:0] rs2Forward
);

  wire and_1_out, and_2_out, and_3_out, and_4_out, and_5_out, and_6_out, and_7_out, and_8_out, and_9_out,
       and_10_out, and_11_out, and_12_out, and_15_out, and_16_out, and_17_out, and_18_out, and_19_out,
       and_20_out, and_21_out, and_22_out, and_23_out, and_24_out, comparator_1_eq, comparator_2_eq,
       comparator_3_eq, comparator_4_eq, comparator_5_eq, comparator_6_eq, comparator_7_eq, comparator_8_eq,
       comparator_9_eq, comparator_10_eq, comparator_11_eq, comparator_12_eq, comparator_13_eq,
       comparator_14_eq, comparator_15_eq, comparator_16_eq, ecall1, ecall2, ecall3, ecall4, not_1_out,
       not_2_out, not_3_out, not_4_out, not_5_out, not_6_out, or_2_out, or_4_out;

  Comparator #(.width(5), .mode("twosComplement")) comparator_1 (
    .a({5{1'b0}}), .b(IR[24:20]), .eq(comparator_1_eq));  // open: gt, lt
  Comparator #(.width(5), .mode("twosComplement")) comparator_2 (
    .a(IR[24:20]), .b(EX_rd), .eq(comparator_2_eq));  // open: gt, lt
  Comparator #(.width(5), .mode("twosComplement")) comparator_3 (
    .a(MEM_rd), .b(IR[24:20]), .eq(comparator_3_eq));  // open: gt, lt
  Comparator #(.width(5), .mode("twosComplement")) comparator_4 (
    .a(IR[24:20]), .b({5{1'b0}}), .eq(comparator_4_eq));  // open: gt, lt
  Comparator #(.width(5), .mode("twosComplement")) comparator_5 (
    .a({5{1'b0}}), .b(IR[19:15]), .eq(comparator_5_eq));  // open: gt, lt
  not not_1 (not_1_out, comparator_5_eq);
  Comparator #(.width(5), .mode("twosComplement")) comparator_6 (
    .a(IR[19:15]), .b(EX_rd), .eq(comparator_6_eq));  // open: gt, lt
  Comparator #(.width(5), .mode("twosComplement")) comparator_7 (
    .a(MEM_rd), .b(IR[19:15]), .eq(comparator_7_eq));  // open: gt, lt
  not not_2 (not_2_out, comparator_8_eq);
  Comparator #(.width(5), .mode("twosComplement")) comparator_8 (
    .a(IR[19:15]), .b({5{1'b0}}), .eq(comparator_8_eq));  // open: gt, lt
  not not_3 (not_3_out, comparator_1_eq);
  not not_4 (not_4_out, comparator_4_eq);
  and and_1 (and_1_out, rs1_used, not_1_out);
  and and_2 (and_2_out, not_2_out, rs1_used);
  and and_3 (and_3_out, rs2_used, not_3_out);
  and and_4 (and_4_out, not_4_out, rs2_used);
  and and_5 (and_5_out, and_1_out, EX_RegWrite);
  and and_6 (and_6_out, MEM_RegWrite, and_2_out);
  and and_7 (and_7_out, and_3_out, EX_RegWrite);
  and and_8 (and_8_out, MEM_RegWrite, and_4_out);
  and and_9 (and_9_out, and_5_out, comparator_6_eq);
  or or_1 (rs1Forward[1], and_9_out, ecall1);
  or or_2 (or_2_out, ecall2, and_10_out);
  and and_10 (and_10_out, comparator_7_eq, and_6_out);
  and and_11 (and_11_out, and_7_out, comparator_2_eq);
  or or_3 (rs2Forward[1], and_11_out, ecall3);
  or or_4 (or_4_out, ecall4, and_12_out);
  and and_12 (and_12_out, comparator_3_eq, and_8_out);
  or or_5 (flush, stall, BranchTaken);
  and and_13 (rs1Forward[0], ~rs1Forward[1], or_2_out);  // AND_Gate
  and and_14 (rs2Forward[0], ~rs2Forward[1], or_4_out);  // AND_Gate
  not not_5 (not_5_out, comparator_9_eq);
  Comparator #(.width(5), .mode("twosComplement")) comparator_9 (
    .a({5{1'b0}}), .b(IR[19:15]), .eq(comparator_9_eq));  // open: gt, lt
  Comparator #(.width(5), .mode("twosComplement")) comparator_10 (
    .a(IR[19:15]), .b(EX_rd), .eq(comparator_10_eq));  // open: gt, lt
  Comparator #(.width(5), .mode("twosComplement")) comparator_11 (
    .a(EX_rd), .b(IR[24:20]), .eq(comparator_11_eq));  // open: gt, lt
  Comparator #(.width(5), .mode("twosComplement")) comparator_12 (
    .a(IR[24:20]), .b({5{1'b0}}), .eq(comparator_12_eq));  // open: gt, lt
  not not_6 (not_6_out, comparator_12_eq);
  and and_15 (and_15_out, rs1_used, not_5_out);
  and and_16 (and_16_out, not_6_out, rs2_used);
  and and_17 (and_17_out, EX_RegWrite, ecall);
  and and_18 (and_18_out, ecall, MEM_RegWrite);
  and and_19 (and_19_out, EX_RegWrite, ecall);
  and and_20 (and_20_out, ecall, MEM_RegWrite);
  and and_21 (and_21_out, and_15_out, EX_MemToReg);
  and and_22 (and_22_out, EX_MemToReg, and_16_out);
  and and_23 (and_23_out, and_21_out, comparator_10_eq);
  and and_24 (and_24_out, comparator_11_eq, and_22_out);
  and and_25 (ecall1, and_17_out, comparator_13_eq);
  Comparator #(.width(5), .mode("twosComplement")) comparator_13 (
    .a(EX_rd), .b(5'b10001), .eq(comparator_13_eq));  // open: gt, lt
  and and_26 (ecall2, and_18_out, comparator_14_eq);
  Comparator #(.width(5), .mode("twosComplement")) comparator_14 (
    .a(MEM_rd), .b(5'b10001), .eq(comparator_14_eq));  // open: gt, lt
  and and_27 (ecall3, and_19_out, comparator_15_eq);
  Comparator #(.width(5), .mode("twosComplement")) comparator_15 (
    .a(EX_rd), .b(5'b01010), .eq(comparator_15_eq));  // open: gt, lt
  and and_28 (ecall4, and_20_out, comparator_16_eq);
  Comparator #(.width(5), .mode("twosComplement")) comparator_16 (
    .a(MEM_rd), .b(5'b01010), .eq(comparator_16_eq));  // open: gt, lt
  or or_6 (stall, and_23_out, and_24_out);

  // Other names for the same wires on the sheet: rs1[4:0] = IR[19:15]; rs2[4:0] = IR[24:20]; LoadUse = stall

  // Notes on the sheet:
  //   重定向处理输入(Input)
  //   重定向数据相关检测
  //   重定向数据处理与输出(Output)
endmodule
